// Logisim project AluPart2.circ as structural Verilog
module J1Bit (
  input  A,
  input  B,
  output out_3
);

  wire and_1_out, and_2_out, not_1_out;

  not not_1 (not_1_out, B);
  and and_1 (and_1_out, A, not_1_out);
  and and_2 (and_2_out, A, B);
  or or_1 (out_3, and_1_out, and_2_out);
endmodule

module Jal1Bit (
  input  A,
  input  B,
  output out_3
);

  wire and_1_out, and_2_out, not_1_out;

  not not_1 (not_1_out, B);
  and and_1 (and_1_out, A, not_1_out);
  and and_2 (and_2_out, A, B);
  or or_1 (out_3, and_1_out, and_2_out);
endmodule

module JR1Bit (
  input  A,
  input  B,
  output out_3
);

  wire and_1_out, and_2_out, not_1_out;

  not not_1 (not_1_out, B);
  and and_1 (and_1_out, A, not_1_out);
  and and_2 (and_2_out, A, B);
  or or_1 (out_3, and_1_out, and_2_out);
endmodule

module Move1Bit (
  input  A,
  input  B,
  output out_3
);

  wire and_1_out, and_2_out, not_1_out;

  not not_1 (not_1_out, B);
  and and_1 (and_1_out, A, not_1_out);
  and and_2 (and_2_out, A, B);
  or or_1 (out_3, and_1_out, and_2_out);
endmodule

module LI1Bit (
  input  A,
  input  B,
  output out_3
);

  wire and_1_out, and_2_out, not_1_out;

  not not_1 (not_1_out, B);
  and and_1 (and_1_out, A, not_1_out);
  and and_2 (and_2_out, A, B);
  or or_1 (out_3, and_1_out, and_2_out);
endmodule

module LA1Bit (
  input  A,
  input  B,
  output out_3
);

  wire and_1_out, and_2_out, not_1_out;

  not not_1 (not_1_out, B);
  and and_1 (and_1_out, A, not_1_out);
  and and_2 (and_2_out, A, B);
  or or_1 (out_3, and_1_out, and_2_out);
endmodule

module Lw1Bit (
  input  A,
  input  B,
  output out_3
);

  wire and_1_out, and_2_out, not_1_out;

  not not_1 (not_1_out, B);
  and and_1 (and_1_out, A, not_1_out);
  and and_2 (and_2_out, A, B);
  or or_1 (out_3, and_1_out, and_2_out);
endmodule

module Sw1Bit (
  input  A,
  input  B,
  output out_3
);

  wire and_1_out, and_2_out, not_1_out;

  not not_1 (not_1_out, B);
  and and_1 (and_1_out, A, not_1_out);
  and and_2 (and_2_out, A, B);
  or or_1 (out_3, and_1_out, and_2_out);
endmodule

module Beq1Bit (
  input  in_1,
  input  in_2,
  output out_3
);

  xnor xnor_1 (out_3, in_1, in_2);
endmodule

module Bne1Bit (
  input  in_1,
  input  in_2,
  output out_3
);

  xor xor_1 (out_3, in_1, in_2);
endmodule

module Bgt1Bit (
  input  in_1,
  input  in_2,
  output out_3
);

  wire not_1_out;

  not not_1 (not_1_out, in_2);
  and and_1 (out_3, in_1, not_1_out);
endmodule

module Blt1Bit (
  input  in_1,
  input  in_2,
  output out_3
);

  wire and_1_out, and_2_out, not_1_out;

  not not_1 (not_1_out, in_1);
  and and_1 (and_1_out, not_1_out, in_2);
  and and_2 (and_2_out, in_1, in_2);
  or or_1 (out_3, and_1_out, and_2_out);
endmodule

module MedioALU1Bit (
  input  [4:0] Opcode,
  input  A,
  input  B,
  output Result
);

  wire beq1bit_1_out_3, bgt1bit_1_out_3, blt1bit_1_out_3, bne1bit_1_out_3, j1bit_1_out_3, jal1bit_1_out_3,
       jr1bit_1_out_3, la1bit_1_out_3, li1bit_1_out_3, lw1bit_1_out_3, move1bit_1_out_3, sw1bit_1_out_3;

  J1Bit j1bit_1 (.A(A), .B(B), .out_3(j1bit_1_out_3));
  Jal1Bit jal1bit_1 (.A(A), .B(B), .out_3(jal1bit_1_out_3));
  JR1Bit jr1bit_1 (.A(A), .B(B), .out_3(jr1bit_1_out_3));
  Beq1Bit beq1bit_1 (.in_1(A), .in_2(B), .out_3(beq1bit_1_out_3));
  Bne1Bit bne1bit_1 (.in_1(A), .in_2(B), .out_3(bne1bit_1_out_3));
  Bgt1Bit bgt1bit_1 (.in_1(A), .in_2(B), .out_3(bgt1bit_1_out_3));
  Blt1Bit blt1bit_1 (.in_1(A), .in_2(B), .out_3(blt1bit_1_out_3));
  Move1Bit move1bit_1 (.A(A), .B(B), .out_3(move1bit_1_out_3));
  LI1Bit li1bit_1 (.A(A), .B(B), .out_3(li1bit_1_out_3));
  LA1Bit la1bit_1 (.A(A), .B(B), .out_3(la1bit_1_out_3));
  Lw1Bit lw1bit_1 (.A(A), .B(B), .out_3(lw1bit_1_out_3));
  Sw1Bit sw1bit_1 (.A(A), .B(B), .out_3(sw1bit_1_out_3));
  Multiplexer #(.select(5), .enable("false")) multiplexer_1 (
    .in11(j1bit_1_out_3), .in12(jal1bit_1_out_3), .in13(jr1bit_1_out_3), .in14(beq1bit_1_out_3),
    .in15(bne1bit_1_out_3), .in16(bgt1bit_1_out_3), .in17(blt1bit_1_out_3), .in18(move1bit_1_out_3),
    .in19(li1bit_1_out_3), .in20(la1bit_1_out_3), .in21(lw1bit_1_out_3), .in22(sw1bit_1_out_3), .out(Result),
    .sel(Opcode));  // open: in0, in1, in2, in3, in4, in5, in6, in7, in8, in9, in10, in23, in24, in25, in26, in27, in28, in29, in30, in31
endmodule

module MedioALU32Bits (
  input  [4:0] Opcode,
  input  [31:0] A,
  input  [31:0] B,
  output [31:0] OutputMedioALU,
  output ZeroFlag
);

  MedioALU1Bit medioalu1bit_1 (.Opcode(Opcode), .A(A[0]), .B(B[0]), .Result(OutputMedioALU[0]));
  MedioALU1Bit medioalu1bit_2 (.Opcode(Opcode), .A(A[1]), .B(B[1]), .Result(OutputMedioALU[1]));
  MedioALU1Bit medioalu1bit_3 (.Opcode(Opcode), .A(A[2]), .B(B[2]), .Result(OutputMedioALU[2]));
  MedioALU1Bit medioalu1bit_4 (.Opcode(Opcode), .A(A[3]), .B(B[3]), .Result(OutputMedioALU[3]));
  MedioALU1Bit medioalu1bit_5 (.Opcode(Opcode), .A(A[4]), .B(B[4]), .Result(OutputMedioALU[4]));
  MedioALU1Bit medioalu1bit_6 (.Opcode(Opcode), .A(A[5]), .B(B[5]), .Result(OutputMedioALU[5]));
  MedioALU1Bit medioalu1bit_7 (.Opcode(Opcode), .A(A[6]), .B(B[6]), .Result(OutputMedioALU[6]));
  MedioALU1Bit medioalu1bit_8 (.Opcode(Opcode), .A(A[7]), .B(B[7]), .Result(OutputMedioALU[7]));
  MedioALU1Bit medioalu1bit_9 (.Opcode(Opcode), .A(A[8]), .B(B[8]));  // open: Result
  MedioALU1Bit medioalu1bit_10 (.Opcode(Opcode), .A(A[9]), .B(B[9]), .Result(OutputMedioALU[9]));
  MedioALU1Bit medioalu1bit_11 (.Opcode(Opcode), .A(A[10]), .B(B[10]), .Result(OutputMedioALU[10]));
  MedioALU1Bit medioalu1bit_12 (.Opcode(Opcode), .A(A[11]), .B(B[11]), .Result(OutputMedioALU[11]));
  MedioALU1Bit medioalu1bit_13 (.Opcode(Opcode), .A(A[12]), .B(B[12]), .Result(OutputMedioALU[12]));
  MedioALU1Bit medioalu1bit_14 (.Opcode(Opcode), .A(A[13]), .B(B[13]), .Result(OutputMedioALU[13]));
  MedioALU1Bit medioalu1bit_15 (.Opcode(Opcode), .A(A[14]), .B(B[14]), .Result(OutputMedioALU[14]));
  MedioALU1Bit medioalu1bit_16 (.Opcode(Opcode), .A(A[15]), .B(B[15]), .Result(OutputMedioALU[15]));
  MedioALU1Bit medioalu1bit_17 (.Opcode(Opcode), .A(A[16]), .B(B[16]), .Result(OutputMedioALU[16]));
  MedioALU1Bit medioalu1bit_18 (.Opcode(Opcode), .A(A[17]), .B(B[17]), .Result(OutputMedioALU[17]));
  MedioALU1Bit medioalu1bit_19 (.Opcode(Opcode), .A(A[18]), .B(B[18]), .Result(OutputMedioALU[18]));
  MedioALU1Bit medioalu1bit_20 (.Opcode(Opcode), .A(A[19]), .B(B[19]), .Result(OutputMedioALU[19]));
  MedioALU1Bit medioalu1bit_21 (.Opcode(Opcode), .A(A[20]), .B(B[20]), .Result(OutputMedioALU[20]));
  MedioALU1Bit medioalu1bit_22 (.Opcode(Opcode), .A(A[21]), .B(B[21]), .Result(OutputMedioALU[21]));
  MedioALU1Bit medioalu1bit_23 (.Opcode(Opcode), .A(A[22]), .B(B[22]), .Result(OutputMedioALU[22]));
  MedioALU1Bit medioalu1bit_24 (.Opcode(Opcode), .A(A[23]), .B(B[23]), .Result(OutputMedioALU[23]));
  MedioALU1Bit medioalu1bit_25 (.Opcode(Opcode), .A(A[24]), .B(B[24]), .Result(OutputMedioALU[24]));
  MedioALU1Bit medioalu1bit_26 (.Opcode(Opcode), .A(A[25]), .B(B[25]), .Result(OutputMedioALU[25]));
  MedioALU1Bit medioalu1bit_27 (.Opcode(Opcode), .A(A[26]), .B(B[26]), .Result(OutputMedioALU[26]));
  MedioALU1Bit medioalu1bit_28 (.Opcode(Opcode), .A(A[27]), .B(B[27]), .Result(OutputMedioALU[27]));
  MedioALU1Bit medioalu1bit_29 (.Opcode(Opcode), .A(A[28]), .B(B[28]), .Result(OutputMedioALU[28]));
  MedioALU1Bit medioalu1bit_30 (.Opcode(Opcode), .A(A[29]), .B(B[29]), .Result(OutputMedioALU[29]));
  MedioALU1Bit medioalu1bit_31 (.Opcode(Opcode), .A(A[30]), .B(B[30]), .Result(OutputMedioALU[30]));
  MedioALU1Bit medioalu1bit_32 (.Opcode(Opcode), .A(A[31]), .B(B[31]), .Result(OutputMedioALU[31]));
  nor nor_1 (ZeroFlag, OutputMedioALU[0], OutputMedioALU[1], OutputMedioALU[2], OutputMedioALU[3], OutputMedioALU[4], OutputMedioALU[5], OutputMedioALU[6], OutputMedioALU[7], OutputMedioALU[8], OutputMedioALU[9], OutputMedioALU[10], OutputMedioALU[11], OutputMedioALU[12], OutputMedioALU[13], OutputMedioALU[14], OutputMedioALU[15], OutputMedioALU[16], OutputMedioALU[17], OutputMedioALU[18], OutputMedioALU[19], OutputMedioALU[20], OutputMedioALU[21], OutputMedioALU[22], OutputMedioALU[23], OutputMedioALU[24], OutputMedioALU[25], OutputMedioALU[26], OutputMedioALU[27], OutputMedioALU[28], OutputMedioALU[29], OutputMedioALU[30], OutputMedioALU[31]);
endmodule
