// Logisim project CUMainControl.circ as structural Verilog
module CUMainController (
  input  [5:0] Opcode,
  output Jump,
  output RegDest,
  output BNEout,
  output BEQout,
  output MemWrite,
  output MemRead,
  output MemToReg,
  output RegWriteOut,
  output ALUSrc,
  output Rtyp,
  output ExtOp,
  output [3:0] ALUop
);

  wire BGT_out, BLT_out, JR_out, LA_out, LI_out, MOVE_out, or_1_out, or_2_out;

  and RType (RegDest, Opcode[5], Opcode[4], Opcode[3], Opcode[2], Opcode[1], Opcode[0]);
  and J (Jump, ~Opcode[5], ~Opcode[4], Opcode[3], Opcode[2], ~Opcode[1], ~Opcode[0]);  // AND_Gate
  // AND_Gate JAL has open pins: in0=Opcode[5], in1=Opcode[4], in2=Opcode[3], in3=Opcode[2], in4=Opcode[1], in5=Opcode[0], out=open
  and JR (JR_out, ~Opcode[5], ~Opcode[4], Opcode[3], Opcode[2], Opcode[1], ~Opcode[0]);  // AND_Gate
  and BEQ (BEQout, ~Opcode[5], ~Opcode[4], Opcode[3], Opcode[2], Opcode[1], Opcode[0]);  // AND_Gate
  and BNE (BNEout, ~Opcode[5], Opcode[4], ~Opcode[3], ~Opcode[2], ~Opcode[1], ~Opcode[0]);  // AND_Gate
  and BGT (BGT_out, ~Opcode[5], Opcode[4], ~Opcode[3], ~Opcode[2], ~Opcode[1], Opcode[0]);  // AND_Gate
  and BLT (BLT_out, ~Opcode[5], Opcode[4], ~Opcode[3], ~Opcode[2], Opcode[1], ~Opcode[0]);  // AND_Gate
  or or_1 (or_1_out, BEQout, BNEout);
  or or_2 (or_2_out, MemRead, MemWrite);
  and MOVE (MOVE_out, ~Opcode[5], Opcode[4], ~Opcode[3], ~Opcode[2], Opcode[1], Opcode[0]);  // AND_Gate
  and LI (LI_out, ~Opcode[5], Opcode[4], ~Opcode[3], Opcode[2], ~Opcode[1], ~Opcode[0]);  // AND_Gate
  and LA (LA_out, ~Opcode[5], Opcode[4], ~Opcode[3], Opcode[2], ~Opcode[1], Opcode[0]);  // AND_Gate
  and LW (MemRead, ~Opcode[5], Opcode[4], ~Opcode[3], Opcode[2], Opcode[1], ~Opcode[0]);  // AND_Gate
  Priority_Encoder #(.select(4)) priority_encoder_1 (
    .in0(or_2_out), .in2(or_1_out), .out(ALUop));  // open: in1, in3, in4, in5, in6, in7, in8, in9, in10, in11, in12, in13, in14, in15, gs, en_out, en_in
  and SW (MemWrite, ~Opcode[5], Opcode[4], ~Opcode[3], Opcode[2], Opcode[1], Opcode[0]);  // AND_Gate
  or RegWrite (RegWriteOut, MemRead, RegDest);
  nor nor_1 (ALUSrc, BNEout, BEQout, RegDest);
  // NOR_Gate nor_2 has open pins: out=ExtOp

  assign MemToReg = MemRead;
  assign Rtyp = RegDest;
endmodule

module CUAluControl (
  input  [3:0] MainCTRL,
  input  [5:0] FUnct,
  input  RType,
  output Sub,
  output [2:0] ALUCtrl
);

  wire ADDa_out, ANDa_out, priority_encoder_1_p2, priority_encoder_1_p3, priority_encoder_1_p7, SUBa_out;
  wire [3:0] multiplexer_1_out;

  Multiplexer #(.width(4), .enable("false")) multiplexer_1 (
    .in0(MainCTRL), .in1(FUnct[3:0]), .out(multiplexer_1_out), .sel(RType));
  and ADDa (ADDa_out, ~multiplexer_1_out[3], ~multiplexer_1_out[2], ~multiplexer_1_out[1], ~multiplexer_1_out[0]);  // AND_Gate
  and SUBa (SUBa_out, ~multiplexer_1_out[3], ~multiplexer_1_out[2], multiplexer_1_out[1], ~multiplexer_1_out[0]);  // AND_Gate
  and ANDa (ANDa_out, ~multiplexer_1_out[3], multiplexer_1_out[2], ~multiplexer_1_out[1], ~multiplexer_1_out[0]);  // AND_Gate
  // Priority_Encoder #(.select(4), .disabled("Z")) priority_encoder_1: pin names not known; wires that end beside it: ANDa_out, priority_encoder_1_p2, priority_encoder_1_p3, ADDa_out, {Sub, ALUCtrl}, SUBa_out, priority_encoder_1_p7
  and ORa (priority_encoder_1_p2, ~multiplexer_1_out[3], multiplexer_1_out[2], ~multiplexer_1_out[1], multiplexer_1_out[0]);  // AND_Gate
  and XORa (priority_encoder_1_p3, ~multiplexer_1_out[3], multiplexer_1_out[2], multiplexer_1_out[1], ~multiplexer_1_out[0]);  // AND_Gate
  and SLTa (priority_encoder_1_p7, multiplexer_1_out[3], ~multiplexer_1_out[2], multiplexer_1_out[1], ~multiplexer_1_out[0]);  // AND_Gate
endmodule

module PCController (
  input  Zero,
  input  Jump,
  input  BNE,
  input  BEQ,
  output [1:0] PC
);

  wire and_1_out, and_2_out;

  and and_1 (and_1_out, ~Zero, BNE);  // AND_Gate
  or or_1 (PC[0], and_1_out, and_2_out);
  and and_2 (and_2_out, Zero, BEQ);

  assign PC[1] = Jump;
endmodule
