// Logisim project RegisterFile.circ as structural Verilog: 7 circuits, main circuit RegisterFile
module RegisterFile (
  input  [4:0] ReadSelectorA,
  input  CLK,
  input  WriteEnable,
  input  [4:0] WriteSelector,
  input  [31:0] WriteData,
  input  [4:0] ReadSelectorB,
  output [31:0] DataOutputA,
  output [31:0] DataOutputB
);

  wire and_1_out, and_2_out, and_3_out, and_4_out, and_5_out, and_6_out, and_7_out, and_8_out, and_9_out,
       and_10_out, and_11_out, and_12_out, and_13_out, and_14_out, and_15_out, and_16_out, and_17_out,
       and_18_out, and_19_out, and_20_out, and_21_out, and_22_out, and_23_out, and_24_out, and_25_out,
       and_26_out, and_27_out, and_28_out, and_29_out, and_30_out, and_31_out, and_32_out, decoder_1_out0,
       decoder_1_out1, decoder_1_out2, decoder_1_out3, decoder_1_out4, decoder_1_out5, decoder_1_out6,
       decoder_1_out7, decoder_1_out8, decoder_1_out9, decoder_1_out10, decoder_1_out11, decoder_1_out12,
       decoder_1_out13, decoder_1_out14, decoder_1_out15, decoder_1_out16, decoder_1_out17, decoder_1_out18,
       decoder_1_out19, decoder_1_out20, decoder_1_out21, decoder_1_out22, decoder_1_out23, decoder_1_out24,
       decoder_1_out25, decoder_1_out26, decoder_1_out27, decoder_1_out28, decoder_1_out29, decoder_1_out30,
       decoder_1_out31;
  wire [31:0] a0_out_3, a1_out_3, a2_out_3, a3_out_3, at_out_3, fp_out_3, gp_out_3, k0_out_3, k1_out_3,
       ra_out_3, s0_out_3, s1_out_3, s2_out_3, s3_out_3, s4_out_3, s5_out_3, s6_out_3, s7_out_3, sp_out_3,
       t0_out_3, t1_out_3, t2_out_3, t3_out_3, t4_out_3, t5_out_3, t6_out_3, t7_out_3, t8_out_3, t9_out_3,
       v0_out_3, v1_out_3, zero_out_3;

  Decoder #(.select(5)) decoder_1 (
    .out0(decoder_1_out0), .out1(decoder_1_out1), .out2(decoder_1_out2), .out3(decoder_1_out3),
    .out4(decoder_1_out4), .out5(decoder_1_out5), .out6(decoder_1_out6), .out7(decoder_1_out7),
    .out8(decoder_1_out8), .out9(decoder_1_out9), .out10(decoder_1_out10), .out11(decoder_1_out11),
    .out12(decoder_1_out12), .out13(decoder_1_out13), .out14(decoder_1_out14), .out15(decoder_1_out15),
    .out16(decoder_1_out16), .out17(decoder_1_out17), .out18(decoder_1_out18), .out19(decoder_1_out19),
    .out20(decoder_1_out20), .out21(decoder_1_out21), .out22(decoder_1_out22), .out23(decoder_1_out23),
    .out24(decoder_1_out24), .out25(decoder_1_out25), .out26(decoder_1_out26), .out27(decoder_1_out27),
    .out28(decoder_1_out28), .out29(decoder_1_out29), .out30(decoder_1_out30), .out31(decoder_1_out31),
    .sel(WriteSelector), .en(WriteEnable));
  and and_1 (and_1_out, CLK, decoder_1_out0);
  and and_2 (and_2_out, CLK, decoder_1_out1);
  and and_3 (and_3_out, CLK, decoder_1_out2);
  and and_4 (and_4_out, CLK, decoder_1_out3);
  and and_5 (and_5_out, CLK, decoder_1_out4);
  and and_6 (and_6_out, CLK, decoder_1_out5);
  and and_7 (and_7_out, CLK, decoder_1_out6);
  and and_8 (and_8_out, CLK, decoder_1_out7);
  ThirtyTwoDFlipFlop zero (.D(WriteData), .CLK(and_1_out), .out_3(zero_out_3));
  ThirtyTwoDFlipFlop at (.D(WriteData), .CLK(and_2_out), .out_3(at_out_3));
  ThirtyTwoDFlipFlop v0 (.D(WriteData), .CLK(and_3_out), .out_3(v0_out_3));
  ThirtyTwoDFlipFlop v1 (.D(WriteData), .CLK(and_4_out), .out_3(v1_out_3));
  ThirtyTwoDFlipFlop a0 (.D(WriteData), .CLK(and_5_out), .out_3(a0_out_3));
  ThirtyTwoDFlipFlop a1 (.D(WriteData), .CLK(and_6_out), .out_3(a1_out_3));
  ThirtyTwoDFlipFlop a2 (.D(WriteData), .CLK(and_7_out), .out_3(a2_out_3));
  ThirtyTwoDFlipFlop a3 (.D(WriteData), .CLK(and_8_out), .out_3(a3_out_3));
  and and_9 (and_9_out, CLK, decoder_1_out8);
  and and_10 (and_10_out, CLK, decoder_1_out9);
  and and_11 (and_11_out, CLK, decoder_1_out10);
  and and_12 (and_12_out, CLK, decoder_1_out11);
  and and_13 (and_13_out, CLK, decoder_1_out12);
  and and_14 (and_14_out, CLK, decoder_1_out13);
  and and_15 (and_15_out, CLK, decoder_1_out14);
  and and_16 (and_16_out, CLK, decoder_1_out15);
  ThirtyTwoDFlipFlop t0 (.D(WriteData), .CLK(and_9_out), .out_3(t0_out_3));
  ThirtyTwoDFlipFlop t1 (.D(WriteData), .CLK(and_10_out), .out_3(t1_out_3));
  ThirtyTwoDFlipFlop t2 (.D(WriteData), .CLK(and_11_out), .out_3(t2_out_3));
  ThirtyTwoDFlipFlop t3 (.D(WriteData), .CLK(and_12_out), .out_3(t3_out_3));
  ThirtyTwoDFlipFlop t4 (.D(WriteData), .CLK(and_13_out), .out_3(t4_out_3));
  ThirtyTwoDFlipFlop t5 (.D(WriteData), .CLK(and_14_out), .out_3(t5_out_3));
  ThirtyTwoDFlipFlop t6 (.D(WriteData), .CLK(and_15_out), .out_3(t6_out_3));
  ThirtyTwoDFlipFlop t7 (.D(WriteData), .CLK(and_16_out), .out_3(t7_out_3));
  and and_17 (and_17_out, CLK, decoder_1_out16);
  and and_18 (and_18_out, CLK, decoder_1_out17);
  and and_19 (and_19_out, CLK, decoder_1_out18);
  and and_20 (and_20_out, CLK, decoder_1_out19);
  and and_21 (and_21_out, CLK, decoder_1_out20);
  and and_22 (and_22_out, CLK, decoder_1_out21);
  and and_23 (and_23_out, CLK, decoder_1_out22);
  and and_24 (and_24_out, CLK, decoder_1_out23);
  ThirtyTwoDFlipFlop t8 (.D(WriteData), .CLK(and_17_out), .out_3(t8_out_3));
  ThirtyTwoDFlipFlop t9 (.D(WriteData), .CLK(and_18_out), .out_3(t9_out_3));
  ThirtyTwoDFlipFlop s0 (.D(WriteData), .CLK(and_19_out), .out_3(s0_out_3));
  ThirtyTwoDFlipFlop s1 (.D(WriteData), .CLK(and_20_out), .out_3(s1_out_3));
  ThirtyTwoDFlipFlop s2 (.D(WriteData), .CLK(and_21_out), .out_3(s2_out_3));
  ThirtyTwoDFlipFlop s3 (.D(WriteData), .CLK(and_22_out), .out_3(s3_out_3));
  ThirtyTwoDFlipFlop s4 (.D(WriteData), .CLK(and_23_out), .out_3(s4_out_3));
  ThirtyTwoDFlipFlop s5 (.D(WriteData), .CLK(and_24_out), .out_3(s5_out_3));
  and and_25 (and_25_out, CLK, decoder_1_out24);
  and and_26 (and_26_out, CLK, decoder_1_out25);
  and and_27 (and_27_out, CLK, decoder_1_out26);
  and and_28 (and_28_out, CLK, decoder_1_out27);
  and and_29 (and_29_out, CLK, decoder_1_out28);
  and and_30 (and_30_out, CLK, decoder_1_out29);
  and and_31 (and_31_out, CLK, decoder_1_out30);
  and and_32 (and_32_out, CLK, decoder_1_out31);
  ThirtyTwoDFlipFlop s6 (.D(WriteData), .CLK(and_25_out), .out_3(s6_out_3));
  ThirtyTwoDFlipFlop s7 (.D(WriteData), .CLK(and_26_out), .out_3(s7_out_3));
  ThirtyTwoDFlipFlop k0 (.D(WriteData), .CLK(and_27_out), .out_3(k0_out_3));
  ThirtyTwoDFlipFlop k1 (.D(WriteData), .CLK(and_28_out), .out_3(k1_out_3));
  ThirtyTwoDFlipFlop gp (.D(WriteData), .CLK(and_29_out), .out_3(gp_out_3));
  ThirtyTwoDFlipFlop sp (.D(WriteData), .CLK(and_30_out), .out_3(sp_out_3));
  ThirtyTwoDFlipFlop fp (.D(WriteData), .CLK(and_31_out), .out_3(fp_out_3));
  ThirtyTwoDFlipFlop ra (.D(WriteData), .CLK(and_32_out), .out_3(ra_out_3));
  Multiplexer #(.select(5), .width(32), .enable("false")) multiplexer_1 (
    .in0(zero_out_3), .in1(at_out_3), .in2(v0_out_3), .in3(v1_out_3), .in4(a0_out_3), .in5(a1_out_3),
    .in6(a2_out_3), .in7(a3_out_3), .in8(t0_out_3), .in9(t1_out_3), .in10(t2_out_3), .in11(t3_out_3),
    .in12(t4_out_3), .in13(t5_out_3), .in14(t6_out_3), .in15(t7_out_3), .in16(t8_out_3), .in17(t9_out_3),
    .in18(s0_out_3), .in19(s1_out_3), .in20(s2_out_3), .in21(s3_out_3), .in22(s4_out_3), .in23(s5_out_3),
    .in24(s6_out_3), .in25(s7_out_3), .in26(k0_out_3), .in27(k1_out_3), .in28(gp_out_3), .in29(sp_out_3),
    .in30(fp_out_3), .in31(ra_out_3), .out(DataOutputA), .sel(ReadSelectorA));
  Multiplexer #(.select(5), .width(32), .enable("false")) multiplexer_2 (
    .in0(zero_out_3), .in1(at_out_3), .in2(v0_out_3), .in3(v1_out_3), .in4(a0_out_3), .in5(a1_out_3),
    .in6(a2_out_3), .in7(a3_out_3), .in8(t0_out_3), .in9(t1_out_3), .in10(t2_out_3), .in11(t3_out_3),
    .in12(t4_out_3), .in13(t5_out_3), .in14(t6_out_3), .in15(t7_out_3), .in16(t8_out_3), .in17(t9_out_3),
    .in18(s0_out_3), .in19(s1_out_3), .in20(s2_out_3), .in21(s3_out_3), .in22(s4_out_3), .in23(s5_out_3),
    .in24(s6_out_3), .in25(s7_out_3), .in26(k0_out_3), .in27(k1_out_3), .in28(gp_out_3), .in29(sp_out_3),
    .in30(fp_out_3), .in31(ra_out_3), .out(DataOutputB), .sel(ReadSelectorB));
  ThirtyTwoDFlipFlop thirtytwodflipflop_1 ();  // open: D, CLK, out_3
  ThirtyTwoDFlipFlop thirtytwodflipflop_2 ();  // open: D, CLK, out_3
  ThirtyTwoDFlipFlop thirtytwodflipflop_3 ();  // open: D, CLK, out_3
endmodule

module DFlipFlop (
  input  D,
  input  CLK,
  output Q
);

  wire nand_1_out, nand_2_out, nand_4_out, not_1_out;

  not not_1 (not_1_out, D);
  nand nand_1 (nand_1_out, D, CLK);
  nand nand_2 (nand_2_out, CLK, not_1_out);
  nand nand_3 (Q, nand_1_out, nand_4_out);
  nand nand_4 (nand_4_out, Q, nand_2_out);
endmodule

module TwoDFlipFlop (
  input  [1:0] D,
  input  CLK,
  output [1:0] Q
);

  DFlipFlop dflipflop_1 (.D(D[0]), .CLK(CLK), .Q(Q[0]));
  DFlipFlop dflipflop_2 (.D(D[1]), .CLK(CLK), .Q(Q[1]));
endmodule

module FourFFlipFlop (
  input  [3:0] D,
  input  CLK,
  output [3:0] Q
);

  TwoDFlipFlop twodflipflop_1 (.D(D[1:0]), .CLK(CLK), .Q(Q[1:0]));
  TwoDFlipFlop twodflipflop_2 (.D(D[3:2]), .CLK(CLK), .Q(Q[3:2]));
endmodule

module EightFlipFlop (
  input  [7:0] D,
  input  CLK,
  output [7:0] Q
);

  FourFFlipFlop fourfflipflop_1 (.D(D[3:0]), .CLK(CLK), .Q(Q[3:0]));
  FourFFlipFlop fourfflipflop_2 (.D(D[7:4]), .CLK(CLK), .Q(Q[7:4]));
endmodule

module SixteenDFlipFlop (
  input  [15:0] D,
  input  CLK,
  output [15:0] Q
);

  EightFlipFlop eightflipflop_1 (.D(D[7:0]), .CLK(CLK), .Q(Q[7:0]));
  EightFlipFlop eightflipflop_2 (.D(D[15:8]), .CLK(CLK), .Q(Q[15:8]));
endmodule

module ThirtyTwoDFlipFlop (
  input  [31:0] D,
  input  CLK,
  output [31:0] out_3
);

  SixteenDFlipFlop sixteendflipflop_1 (.D(D[15:0]), .CLK(CLK), .Q(out_3[15:0]));
  SixteenDFlipFlop sixteendflipflop_2 (.D(D[31:16]), .CLK(CLK), .Q(out_3[31:16]));
endmodule
