// Logisim project cpu.circ as structural Verilog
module RegisterFile (
  input  [4:0] ReadSelectorA,
  input  CLK,
  input  WriteEnable,
  input  [4:0] WriteSelector,
  input  [31:0] WriteData,
  input  [4:0] ReadSelectorB,
  output [31:0] DataOutputA,
  output [31:0] DataOutputB
);

  wire and_1_out, and_2_out, and_3_out, and_4_out, and_5_out, and_6_out, and_7_out, and_8_out, and_9_out,
       and_10_out, and_11_out, and_12_out, and_13_out, and_14_out, and_15_out, and_16_out, and_17_out,
       and_18_out, and_19_out, and_20_out, and_21_out, and_22_out, and_23_out, and_24_out, and_25_out,
       and_26_out, and_27_out, and_28_out, and_29_out, and_30_out, and_31_out, and_32_out, decoder_1_out0,
       decoder_1_out1, decoder_1_out2, decoder_1_out3, decoder_1_out4, decoder_1_out5, decoder_1_out6,
       decoder_1_out7, decoder_1_out8, decoder_1_out9, decoder_1_out10, decoder_1_out11, decoder_1_out12,
       decoder_1_out13, decoder_1_out14, decoder_1_out15, decoder_1_out16, decoder_1_out17, decoder_1_out18,
       decoder_1_out19, decoder_1_out20, decoder_1_out21, decoder_1_out22, decoder_1_out23, decoder_1_out24,
       decoder_1_out25, decoder_1_out26, decoder_1_out27, decoder_1_out28, decoder_1_out29, decoder_1_out30,
       decoder_1_out31;
  wire [31:0] a0_out_3, a1_out_3, a2_out_3, a3_out_3, at_out_3, fp_out_3, gp_out_3, k0_out_3, k1_out_3,
       ra_out_3, s0_out_3, s1_out_3, s2_out_3, s3_out_3, s4_out_3, s5_out_3, s6_out_3, s7_out_3, sp_out_3,
       t0_out_3, t1_out_3, t2_out_3, t3_out_3, t4_out_3, t5_out_3, t6_out_3, t7_out_3, t8_out_3, t9_out_3,
       v0_out_3, v1_out_3, zero_out_3;

  Decoder #(.select(5)) decoder_1 (
    .out0(decoder_1_out0), .out1(decoder_1_out1), .out2(decoder_1_out2), .out3(decoder_1_out3),
    .out4(decoder_1_out4), .out5(decoder_1_out5), .out6(decoder_1_out6), .out7(decoder_1_out7),
    .out8(decoder_1_out8), .out9(decoder_1_out9), .out10(decoder_1_out10), .out11(decoder_1_out11),
    .out12(decoder_1_out12), .out13(decoder_1_out13), .out14(decoder_1_out14), .out15(decoder_1_out15),
    .out16(decoder_1_out16), .out17(decoder_1_out17), .out18(decoder_1_out18), .out19(decoder_1_out19),
    .out20(decoder_1_out20), .out21(decoder_1_out21), .out22(decoder_1_out22), .out23(decoder_1_out23),
    .out24(decoder_1_out24), .out25(decoder_1_out25), .out26(decoder_1_out26), .out27(decoder_1_out27),
    .out28(decoder_1_out28), .out29(decoder_1_out29), .out30(decoder_1_out30), .out31(decoder_1_out31),
    .sel(WriteSelector), .en(WriteEnable));
  and and_1 (and_1_out, CLK, decoder_1_out0);
  and and_2 (and_2_out, CLK, decoder_1_out1);
  and and_3 (and_3_out, CLK, decoder_1_out2);
  and and_4 (and_4_out, CLK, decoder_1_out3);
  and and_5 (and_5_out, CLK, decoder_1_out4);
  and and_6 (and_6_out, CLK, decoder_1_out5);
  and and_7 (and_7_out, CLK, decoder_1_out6);
  and and_8 (and_8_out, CLK, decoder_1_out7);
  ThirtyTwoDFlipFlop zero (.D(WriteData), .CLK(and_1_out), .out_3(zero_out_3));
  ThirtyTwoDFlipFlop at (.D(WriteData), .CLK(and_2_out), .out_3(at_out_3));
  ThirtyTwoDFlipFlop v0 (.D(WriteData), .CLK(and_3_out), .out_3(v0_out_3));
  ThirtyTwoDFlipFlop v1 (.D(WriteData), .CLK(and_4_out), .out_3(v1_out_3));
  ThirtyTwoDFlipFlop a0 (.D(WriteData), .CLK(and_5_out), .out_3(a0_out_3));
  ThirtyTwoDFlipFlop a1 (.D(WriteData), .CLK(and_6_out), .out_3(a1_out_3));
  ThirtyTwoDFlipFlop a2 (.D(WriteData), .CLK(and_7_out), .out_3(a2_out_3));
  ThirtyTwoDFlipFlop a3 (.D(WriteData), .CLK(and_8_out), .out_3(a3_out_3));
  and and_9 (and_9_out, CLK, decoder_1_out8);
  and and_10 (and_10_out, CLK, decoder_1_out9);
  and and_11 (and_11_out, CLK, decoder_1_out10);
  and and_12 (and_12_out, CLK, decoder_1_out11);
  and and_13 (and_13_out, CLK, decoder_1_out12);
  and and_14 (and_14_out, CLK, decoder_1_out13);
  and and_15 (and_15_out, CLK, decoder_1_out14);
  and and_16 (and_16_out, CLK, decoder_1_out15);
  ThirtyTwoDFlipFlop t0 (.D(WriteData), .CLK(and_9_out), .out_3(t0_out_3));
  ThirtyTwoDFlipFlop t1 (.D(WriteData), .CLK(and_10_out), .out_3(t1_out_3));
  ThirtyTwoDFlipFlop t2 (.D(WriteData), .CLK(and_11_out), .out_3(t2_out_3));
  ThirtyTwoDFlipFlop t3 (.D(WriteData), .CLK(and_12_out), .out_3(t3_out_3));
  ThirtyTwoDFlipFlop t4 (.D(WriteData), .CLK(and_13_out), .out_3(t4_out_3));
  ThirtyTwoDFlipFlop t5 (.D(WriteData), .CLK(and_14_out), .out_3(t5_out_3));
  ThirtyTwoDFlipFlop t6 (.D(WriteData), .CLK(and_15_out), .out_3(t6_out_3));
  ThirtyTwoDFlipFlop t7 (.D(WriteData), .CLK(and_16_out), .out_3(t7_out_3));
  and and_17 (and_17_out, CLK, decoder_1_out16);
  and and_18 (and_18_out, CLK, decoder_1_out17);
  and and_19 (and_19_out, CLK, decoder_1_out18);
  and and_20 (and_20_out, CLK, decoder_1_out19);
  and and_21 (and_21_out, CLK, decoder_1_out20);
  and and_22 (and_22_out, CLK, decoder_1_out21);
  and and_23 (and_23_out, CLK, decoder_1_out22);
  and and_24 (and_24_out, CLK, decoder_1_out23);
  ThirtyTwoDFlipFlop t8 (.D(WriteData), .CLK(and_17_out), .out_3(t8_out_3));
  ThirtyTwoDFlipFlop t9 (.D(WriteData), .CLK(and_18_out), .out_3(t9_out_3));
  ThirtyTwoDFlipFlop s0 (.D(WriteData), .CLK(and_19_out), .out_3(s0_out_3));
  ThirtyTwoDFlipFlop s1 (.D(WriteData), .CLK(and_20_out), .out_3(s1_out_3));
  ThirtyTwoDFlipFlop s2 (.D(WriteData), .CLK(and_21_out), .out_3(s2_out_3));
  ThirtyTwoDFlipFlop s3 (.D(WriteData), .CLK(and_22_out), .out_3(s3_out_3));
  ThirtyTwoDFlipFlop s4 (.D(WriteData), .CLK(and_23_out), .out_3(s4_out_3));
  ThirtyTwoDFlipFlop s5 (.D(WriteData), .CLK(and_24_out), .out_3(s5_out_3));
  and and_25 (and_25_out, CLK, decoder_1_out24);
  and and_26 (and_26_out, CLK, decoder_1_out25);
  and and_27 (and_27_out, CLK, decoder_1_out26);
  and and_28 (and_28_out, CLK, decoder_1_out27);
  and and_29 (and_29_out, CLK, decoder_1_out28);
  and and_30 (and_30_out, CLK, decoder_1_out29);
  and and_31 (and_31_out, CLK, decoder_1_out30);
  and and_32 (and_32_out, CLK, decoder_1_out31);
  ThirtyTwoDFlipFlop s6 (.D(WriteData), .CLK(and_25_out), .out_3(s6_out_3));
  ThirtyTwoDFlipFlop s7 (.D(WriteData), .CLK(and_26_out), .out_3(s7_out_3));
  ThirtyTwoDFlipFlop k0 (.D(WriteData), .CLK(and_27_out), .out_3(k0_out_3));
  ThirtyTwoDFlipFlop k1 (.D(WriteData), .CLK(and_28_out), .out_3(k1_out_3));
  ThirtyTwoDFlipFlop gp (.D(WriteData), .CLK(and_29_out), .out_3(gp_out_3));
  ThirtyTwoDFlipFlop sp (.D(WriteData), .CLK(and_30_out), .out_3(sp_out_3));
  ThirtyTwoDFlipFlop fp (.D(WriteData), .CLK(and_31_out), .out_3(fp_out_3));
  ThirtyTwoDFlipFlop ra (.D(WriteData), .CLK(and_32_out), .out_3(ra_out_3));
  Multiplexer #(.select(5), .width(32), .enable("false")) multiplexer_1 (
    .in0(zero_out_3), .in1(at_out_3), .in2(v0_out_3), .in3(v1_out_3), .in4(a0_out_3), .in5(a1_out_3),
    .in6(a2_out_3), .in7(a3_out_3), .in8(t0_out_3), .in9(t1_out_3), .in10(t2_out_3), .in11(t3_out_3),
    .in12(t4_out_3), .in13(t5_out_3), .in14(t6_out_3), .in15(t7_out_3), .in16(t8_out_3), .in17(t9_out_3),
    .in18(s0_out_3), .in19(s1_out_3), .in20(s2_out_3), .in21(s3_out_3), .in22(s4_out_3), .in23(s5_out_3),
    .in24(s6_out_3), .in25(s7_out_3), .in26(k0_out_3), .in27(k1_out_3), .in28(gp_out_3), .in29(sp_out_3),
    .in30(fp_out_3), .in31(ra_out_3), .out(DataOutputA), .sel(ReadSelectorA));
  Multiplexer #(.select(5), .width(32), .enable("false")) multiplexer_2 (
    .in0(zero_out_3), .in1(at_out_3), .in2(v0_out_3), .in3(v1_out_3), .in4(a0_out_3), .in5(a1_out_3),
    .in6(a2_out_3), .in7(a3_out_3), .in8(t0_out_3), .in9(t1_out_3), .in10(t2_out_3), .in11(t3_out_3),
    .in12(t4_out_3), .in13(t5_out_3), .in14(t6_out_3), .in15(t7_out_3), .in16(t8_out_3), .in17(t9_out_3),
    .in18(s0_out_3), .in19(s1_out_3), .in20(s2_out_3), .in21(s3_out_3), .in22(s4_out_3), .in23(s5_out_3),
    .in24(s6_out_3), .in25(s7_out_3), .in26(k0_out_3), .in27(k1_out_3), .in28(gp_out_3), .in29(sp_out_3),
    .in30(fp_out_3), .in31(ra_out_3), .out(DataOutputB), .sel(ReadSelectorB));

  // Notes on the sheet:
  //   Juan Jose Elgueta
  //   Abner Xocop
endmodule

module DFlipFlop (
  input  D,
  input  CLK,
  output Q
);

  wire nand_1_out, nand_2_out, nand_4_out, not_1_out;

  not not_1 (not_1_out, D);
  nand nand_1 (nand_1_out, D, CLK);
  nand nand_2 (nand_2_out, CLK, not_1_out);
  nand nand_3 (Q, nand_1_out, nand_4_out);
  nand nand_4 (nand_4_out, Q, nand_2_out);
endmodule

module TwoDFlipFlop (
  input  [1:0] D,
  input  CLK,
  output [1:0] Q
);

  DFlipFlop dflipflop_1 (.D(D[0]), .CLK(CLK), .Q(Q[0]));
  DFlipFlop dflipflop_2 (.D(D[1]), .CLK(CLK), .Q(Q[1]));
endmodule

module FourFFlipFlop (
  input  [3:0] D,
  input  CLK,
  output [3:0] Q
);

  TwoDFlipFlop twodflipflop_1 (.D(D[1:0]), .CLK(CLK), .Q(Q[1:0]));
  TwoDFlipFlop twodflipflop_2 (.D(D[3:2]), .CLK(CLK), .Q(Q[3:2]));
endmodule

module EightFlipFlop (
  input  [7:0] D,
  input  CLK,
  output [7:0] Q
);

  FourFFlipFlop fourfflipflop_1 (.D(D[3:0]), .CLK(CLK), .Q(Q[3:0]));
  FourFFlipFlop fourfflipflop_2 (.D(D[7:4]), .CLK(CLK), .Q(Q[7:4]));
endmodule

module SixteenDFlipFlop (
  input  [15:0] D,
  input  CLK,
  output [15:0] Q
);

  EightFlipFlop eightflipflop_1 (.D(D[7:0]), .CLK(CLK), .Q(Q[7:0]));
  EightFlipFlop eightflipflop_2 (.D(D[15:8]), .CLK(CLK), .Q(Q[15:8]));
endmodule

module ThirtyTwoDFlipFlop (
  input  [31:0] D,
  input  CLK,
  output [31:0] out_3
);

  SixteenDFlipFlop sixteendflipflop_1 (.D(D[15:0]), .CLK(CLK), .Q(out_3[15:0]));
  SixteenDFlipFlop sixteendflipflop_2 (.D(D[31:16]), .CLK(CLK), .Q(out_3[31:16]));
endmodule

module FullAdder (
  input  Ci,
  input  A,
  input  B,
  output R,
  output Co
);

  wire and_1_out, and_2_out, and_3_out, xor_1_out;

  xor xor_1 (xor_1_out, Ci, A);
  and and_1 (and_1_out, A, Ci);
  and and_2 (and_2_out, A, B);
  and and_3 (and_3_out, Ci, B);
  xor xor_2 (R, xor_1_out, B);
  or or_1 (Co, and_1_out, and_2_out, and_3_out);
endmodule

module FourBitAdder (
  input  Ci,
  input  A0,
  input  B0,
  input  A1,
  input  B1,
  input  A2,
  input  B2,
  input  A3,
  input  B3,
  output R0,
  output R1,
  output R2,
  output R3,
  output Co
);

  wire fulladder_1_co, fulladder_2_co, fulladder_3_co;

  FullAdder fulladder_1 (.Ci(Ci), .A(A0), .B(B0), .R(R0), .Co(fulladder_1_co));
  FullAdder fulladder_2 (.Ci(fulladder_1_co), .A(A1), .B(B1), .R(R1), .Co(fulladder_2_co));
  FullAdder fulladder_3 (.Ci(fulladder_2_co), .A(A2), .B(B2), .R(R2), .Co(fulladder_3_co));
  FullAdder fulladder_4 (.Ci(fulladder_3_co), .A(A3), .B(B3), .R(R3), .Co(Co));
endmodule

module EightBitAdder (
  input  Ci,
  input  A0,
  input  B0,
  input  A1,
  input  B1,
  input  A2,
  input  B2,
  input  A3,
  input  B3,
  input  A4,
  input  B4,
  input  A5,
  input  B5,
  input  A6,
  input  B6,
  input  A7,
  input  B7,
  output R0,
  output R1,
  output R2,
  output R3,
  output R4,
  output R5,
  output R6,
  output R7,
  output Co
);

  wire fourbitadder_1_co;

  FourBitAdder fourbitadder_1 (
    .Ci(Ci), .A0(A0), .B0(B0), .A1(A1), .B1(B1), .A2(A2), .B2(B2), .A3(A3), .B3(B3), .R0(R0), .R1(R1),
    .R2(R2), .R3(R3), .Co(fourbitadder_1_co));
  FourBitAdder fourbitadder_2 (
    .Ci(fourbitadder_1_co), .A0(A4), .B0(B4), .A1(A5), .B1(B5), .A2(A6), .B2(B6), .A3(A7), .B3(B7), .R0(R4),
    .R1(R5), .R2(R6), .R3(R7), .Co(Co));
endmodule

module SixteenBitAdder (
  input  Ci,
  input  A0,
  input  B0,
  input  A1,
  input  B1,
  input  A2,
  input  B2,
  input  A3,
  input  B3,
  input  A4,
  input  B4,
  input  A5,
  input  B5,
  input  A6,
  input  B6,
  input  A7,
  input  B7,
  input  A8,
  input  B8,
  input  A9,
  input  B9,
  input  A10,
  input  B10,
  input  A11,
  input  B11,
  input  A12,
  input  B12,
  input  A13,
  input  B13,
  input  A14,
  input  B14,
  input  A15,
  input  B15,
  output R0,
  output R1,
  output R2,
  output R3,
  output R4,
  output R5,
  output R6,
  output R7,
  output R8,
  output R9,
  output R10,
  output R11,
  output R12,
  output R13,
  output R14,
  output R15,
  output Co
);

  wire eightbitadder_1_co;

  EightBitAdder eightbitadder_1 (
    .Ci(Ci), .A0(A0), .B0(B0), .A1(A1), .B1(B1), .A2(A2), .B2(B2), .A3(A3), .B3(B3), .A4(A4), .B4(B4),
    .A5(A5), .B5(B5), .A6(A6), .B6(B6), .A7(A7), .B7(B7), .R0(R0), .R1(R1), .R2(R2), .R3(R3), .R4(R4),
    .R5(R5), .R6(R6), .R7(R7), .Co(eightbitadder_1_co));
  EightBitAdder eightbitadder_2 (
    .Ci(eightbitadder_1_co), .A0(A8), .B0(B8), .A1(A9), .B1(B9), .A2(A10), .B2(B10), .A3(A11), .B3(B11),
    .A4(A12), .B4(B12), .A5(A13), .B5(B13), .A6(A14), .B6(B14), .A7(A15), .B7(B15), .R0(R8), .R1(R9),
    .R2(R10), .R3(R11), .R4(R12), .R5(R13), .R6(R14), .R7(R15), .Co(Co));
endmodule

module ThirtyTwoBitAdder (
  input  Ci,
  input  [31:0] A,
  input  [31:0] B,
  output [31:0] R,
  output Co
);

  wire sixteenbitadder_1_co;

  SixteenBitAdder sixteenbitadder_1 (
    .Ci(Ci), .A0(A[0]), .B0(B[0]), .A1(A[1]), .B1(B[1]), .A2(A[2]), .B2(B[2]), .A3(A[3]), .B3(B[3]),
    .A4(A[4]), .B4(B[4]), .A5(A[5]), .B5(B[5]), .A6(A[6]), .B6(B[6]), .A7(A[7]), .B7(B[7]), .A8(A[8]),
    .B8(B[8]), .A9(A[9]), .B9(B[9]), .A10(A[10]), .B10(B[10]), .A11(A[11]), .B11(B[11]), .A12(A[12]),
    .B12(B[12]), .A13(A[13]), .B13(B[13]), .A14(A[14]), .B14(B[14]), .A15(A[15]), .B15(B[15]), .R0(R[0]),
    .R1(R[1]), .R2(R[2]), .R3(R[3]), .R4(R[4]), .R5(R[5]), .R6(R[6]), .R7(R[7]), .R8(R[8]), .R9(R[9]),
    .R10(R[10]), .R11(R[11]), .R12(R[12]), .R13(R[13]), .R14(R[14]), .R15(R[15]), .Co(sixteenbitadder_1_co));
  SixteenBitAdder sixteenbitadder_2 (
    .Ci(sixteenbitadder_1_co), .A0(A[16]), .B0(B[16]), .A1(A[17]), .B1(B[17]), .A2(A[18]), .B2(B[18]),
    .A3(A[19]), .B3(B[19]), .A4(A[20]), .B4(B[20]), .A5(A[21]), .B5(B[21]), .A6(A[22]), .B6(B[22]),
    .A7(A[23]), .B7(B[23]), .A8(A[24]), .B8(B[24]), .A9(A[25]), .B9(B[25]), .A10(A[26]), .B10(B[26]),
    .A11(A[27]), .B11(B[27]), .A12(A[28]), .B12(B[28]), .A13(A[29]), .B13(B[29]), .A14(A[30]), .B14(B[30]),
    .A15(A[31]), .B15(B[31]), .R0(R[16]), .R1(R[17]), .R2(R[18]), .R3(R[19]), .R4(R[20]), .R5(R[21]),
    .R6(R[22]), .R7(R[23]), .R8(R[24]), .R9(R[25]), .R10(R[26]), .R11(R[27]), .R12(R[28]), .R13(R[29]),
    .R14(R[30]), .R15(R[31]), .Co(Co));
endmodule

module ThirtyTwoBitSubstraction (
  input  [31:0] A,
  input  [31:0] B,
  output [31:0] R,
  output ALessThanB
);

  wire [31:0] not_1_out;

  assign not_1_out = ~B;  // NOT_Gate not_1, 32 bits wide
  ThirtyTwoBitAdder thirtytwobitadder_1 (.Ci(1'b1), .A(A), .B(not_1_out), .R(R), .Co(ALessThanB));
endmodule

module RShifter (
  input  S0,
  input  [31:0] A,
  input  Si,
  output [31:0] out_4
);

  Multiplexer #(.enable("false")) multiplexer_1 (.in0(A[0]), .in1(A[1]), .out(out_4[0]), .sel(S0));
  Multiplexer #(.enable("false")) multiplexer_2 (.in0(A[1]), .in1(A[2]), .out(out_4[1]), .sel(S0));
  Multiplexer #(.enable("false")) multiplexer_3 (.in0(A[2]), .in1(A[3]), .out(out_4[2]), .sel(S0));
  Multiplexer #(.enable("false")) multiplexer_4 (.in0(A[3]), .in1(A[4]), .out(out_4[3]), .sel(S0));
  Multiplexer #(.enable("false")) multiplexer_5 (.in0(A[4]), .in1(A[5]), .out(out_4[4]), .sel(S0));
  Multiplexer #(.enable("false")) multiplexer_6 (.in0(A[5]), .in1(A[6]), .out(out_4[5]), .sel(S0));
  Multiplexer #(.enable("false")) multiplexer_7 (.in0(A[6]), .in1(A[7]), .out(out_4[6]), .sel(S0));
  Multiplexer #(.enable("false")) multiplexer_8 (.in0(A[7]), .in1(A[8]), .out(out_4[7]), .sel(S0));
  Multiplexer #(.enable("false")) multiplexer_9 (.in0(A[8]), .in1(A[9]), .out(out_4[8]), .sel(S0));
  Multiplexer #(.enable("false")) multiplexer_10 (.in0(A[9]), .in1(A[10]), .out(out_4[9]), .sel(S0));
  Multiplexer #(.enable("false")) multiplexer_11 (.in0(A[10]), .in1(A[11]), .out(out_4[10]), .sel(S0));
  Multiplexer #(.enable("false")) multiplexer_12 (.in0(A[11]), .in1(A[12]), .out(out_4[11]), .sel(S0));
  Multiplexer #(.enable("false")) multiplexer_13 (.in0(A[12]), .in1(A[13]), .out(out_4[12]), .sel(S0));
  Multiplexer #(.enable("false")) multiplexer_14 (.in0(A[13]), .in1(A[14]), .out(out_4[13]), .sel(S0));
  Multiplexer #(.enable("false")) multiplexer_15 (.in0(A[14]), .in1(A[15]), .out(out_4[14]), .sel(S0));
  Multiplexer #(.enable("false")) multiplexer_16 (.in0(A[15]), .in1(A[16]), .out(out_4[15]), .sel(S0));
  Multiplexer #(.enable("false")) multiplexer_17 (.in0(A[16]), .in1(A[17]), .out(out_4[16]), .sel(S0));
  Multiplexer #(.enable("false")) multiplexer_18 (.in0(A[17]), .in1(A[18]), .out(out_4[17]), .sel(S0));
  Multiplexer #(.enable("false")) multiplexer_19 (.in0(A[18]), .in1(A[19]), .out(out_4[18]), .sel(S0));
  Multiplexer #(.enable("false")) multiplexer_20 (.in0(A[19]), .in1(A[20]), .out(out_4[19]), .sel(S0));
  Multiplexer #(.enable("false")) multiplexer_21 (.in0(A[20]), .in1(A[21]), .out(out_4[20]), .sel(S0));
  Multiplexer #(.enable("false")) multiplexer_22 (.in0(A[21]), .in1(A[22]), .out(out_4[21]), .sel(S0));
  Multiplexer #(.enable("false")) multiplexer_23 (.in0(A[22]), .in1(A[23]), .out(out_4[22]), .sel(S0));
  Multiplexer #(.enable("false")) multiplexer_24 (.in0(A[23]), .in1(A[24]), .out(out_4[23]), .sel(S0));
  Multiplexer #(.enable("false")) multiplexer_25 (.in0(A[24]), .in1(A[25]), .out(out_4[24]), .sel(S0));
  Multiplexer #(.enable("false")) multiplexer_26 (.in0(A[25]), .in1(A[26]), .out(out_4[25]), .sel(S0));
  Multiplexer #(.enable("false")) multiplexer_27 (.in0(A[26]), .in1(A[27]), .out(out_4[26]), .sel(S0));
  Multiplexer #(.enable("false")) multiplexer_28 (.in0(A[27]), .in1(A[28]), .out(out_4[27]), .sel(S0));
  Multiplexer #(.enable("false")) multiplexer_29 (.in0(A[28]), .in1(A[29]), .out(out_4[28]), .sel(S0));
  Multiplexer #(.enable("false")) multiplexer_30 (.in0(A[29]), .in1(A[30]), .out(out_4[29]), .sel(S0));
  Multiplexer #(.enable("false")) multiplexer_31 (.in0(A[30]), .in1(A[31]), .out(out_4[30]), .sel(S0));
  Multiplexer #(.enable("false")) multiplexer_32 (.in0(A[31]), .in1(Si), .out(out_4[31]), .sel(S0));
endmodule

module FRShifter (
  input  [4:0] S,
  input  [31:0] A,
  input  Si,
  output [31:0] R
);

  wire multiplexer_1_out, multiplexer_2_out, multiplexer_3_out, multiplexer_4_out, multiplexer_5_out,
       multiplexer_6_out, multiplexer_7_out, multiplexer_8_out, multiplexer_9_out, multiplexer_10_out,
       multiplexer_11_out, multiplexer_12_out, multiplexer_13_out, multiplexer_14_out, multiplexer_15_out,
       multiplexer_16_out, multiplexer_17_out, multiplexer_18_out, multiplexer_19_out, multiplexer_20_out,
       multiplexer_21_out, multiplexer_22_out, multiplexer_23_out, multiplexer_24_out, multiplexer_25_out,
       multiplexer_26_out, multiplexer_27_out, multiplexer_28_out, multiplexer_29_out, multiplexer_30_out,
       multiplexer_31_out, multiplexer_32_out, multiplexer_33_out, multiplexer_34_out, multiplexer_35_out,
       multiplexer_36_out, multiplexer_37_out, multiplexer_38_out, multiplexer_39_out, multiplexer_40_out,
       multiplexer_41_out, multiplexer_42_out, multiplexer_43_out, multiplexer_44_out, multiplexer_45_out,
       multiplexer_46_out, multiplexer_47_out, multiplexer_48_out, multiplexer_49_out, multiplexer_50_out,
       multiplexer_51_out, multiplexer_52_out, multiplexer_53_out, multiplexer_54_out, multiplexer_55_out,
       multiplexer_56_out, multiplexer_57_out, multiplexer_58_out, multiplexer_59_out, multiplexer_60_out,
       multiplexer_61_out, multiplexer_62_out, multiplexer_63_out, multiplexer_64_out, multiplexer_65_out,
       multiplexer_66_out, multiplexer_67_out, multiplexer_68_out, multiplexer_69_out, multiplexer_70_out,
       multiplexer_71_out, multiplexer_72_out, multiplexer_73_out, multiplexer_74_out, multiplexer_75_out,
       multiplexer_76_out, multiplexer_77_out, multiplexer_78_out, multiplexer_79_out, multiplexer_80_out,
       multiplexer_81_out, multiplexer_82_out, multiplexer_83_out, multiplexer_84_out, multiplexer_85_out,
       multiplexer_86_out, multiplexer_87_out, multiplexer_88_out, multiplexer_89_out, multiplexer_90_out,
       multiplexer_91_out, multiplexer_92_out, multiplexer_93_out, multiplexer_94_out, multiplexer_95_out,
       multiplexer_96_out, multiplexer_97_out, multiplexer_98_out, multiplexer_99_out, multiplexer_100_out,
       multiplexer_101_out, multiplexer_102_out, multiplexer_103_out, multiplexer_104_out,
       multiplexer_105_out, multiplexer_106_out, multiplexer_107_out, multiplexer_108_out,
       multiplexer_109_out, multiplexer_110_out, multiplexer_111_out, multiplexer_112_out,
       multiplexer_113_out, multiplexer_114_out, multiplexer_115_out, multiplexer_116_out,
       multiplexer_117_out, multiplexer_118_out, multiplexer_119_out, multiplexer_120_out,
       multiplexer_121_out, multiplexer_122_out, multiplexer_123_out, multiplexer_124_out,
       multiplexer_125_out, multiplexer_126_out, multiplexer_127_out, multiplexer_128_out;

  Multiplexer #(.enable("false")) multiplexer_1 (.in0(A[0]), .in1(A[1]), .out(multiplexer_1_out), .sel(S[0]));
  Multiplexer #(.enable("false")) multiplexer_2 (.in0(A[1]), .in1(A[2]), .out(multiplexer_2_out), .sel(S[0]));
  Multiplexer #(.enable("false")) multiplexer_3 (.in0(A[2]), .in1(A[3]), .out(multiplexer_3_out), .sel(S[0]));
  Multiplexer #(.enable("false")) multiplexer_4 (.in0(A[3]), .in1(A[4]), .out(multiplexer_4_out), .sel(S[0]));
  Multiplexer #(.enable("false")) multiplexer_5 (.in0(A[4]), .in1(A[5]), .out(multiplexer_5_out), .sel(S[0]));
  Multiplexer #(.enable("false")) multiplexer_6 (.in0(A[5]), .in1(A[6]), .out(multiplexer_6_out), .sel(S[0]));
  Multiplexer #(.enable("false")) multiplexer_7 (.in0(A[6]), .in1(A[7]), .out(multiplexer_7_out), .sel(S[0]));
  Multiplexer #(.enable("false")) multiplexer_8 (.in0(A[7]), .in1(A[8]), .out(multiplexer_8_out), .sel(S[0]));
  Multiplexer #(.enable("false")) multiplexer_9 (.in0(A[8]), .in1(A[9]), .out(multiplexer_9_out), .sel(S[0]));
  Multiplexer #(.enable("false")) multiplexer_10 (.in0(A[9]), .in1(A[10]), .out(multiplexer_10_out), .sel(S[0]));
  Multiplexer #(.enable("false")) multiplexer_11 (.in0(A[10]), .in1(A[11]), .out(multiplexer_11_out), .sel(S[0]));
  Multiplexer #(.enable("false")) multiplexer_12 (.in0(A[11]), .in1(A[12]), .out(multiplexer_12_out), .sel(S[0]));
  Multiplexer #(.enable("false")) multiplexer_13 (.in0(A[12]), .in1(A[13]), .out(multiplexer_13_out), .sel(S[0]));
  Multiplexer #(.enable("false")) multiplexer_14 (.in0(A[13]), .in1(A[14]), .out(multiplexer_14_out), .sel(S[0]));
  Multiplexer #(.enable("false")) multiplexer_15 (.in0(A[14]), .in1(A[15]), .out(multiplexer_15_out), .sel(S[0]));
  Multiplexer #(.enable("false")) multiplexer_16 (.in0(A[15]), .in1(A[16]), .out(multiplexer_16_out), .sel(S[0]));
  Multiplexer #(.enable("false")) multiplexer_17 (.in0(A[16]), .in1(A[17]), .out(multiplexer_17_out), .sel(S[0]));
  Multiplexer #(.enable("false")) multiplexer_18 (.in0(A[17]), .in1(A[18]), .out(multiplexer_18_out), .sel(S[0]));
  Multiplexer #(.enable("false")) multiplexer_19 (.in0(A[18]), .in1(A[19]), .out(multiplexer_19_out), .sel(S[0]));
  Multiplexer #(.enable("false")) multiplexer_20 (.in0(A[19]), .in1(A[20]), .out(multiplexer_20_out), .sel(S[0]));
  Multiplexer #(.enable("false")) multiplexer_21 (.in0(A[20]), .in1(A[21]), .out(multiplexer_21_out), .sel(S[0]));
  Multiplexer #(.enable("false")) multiplexer_22 (.in0(A[21]), .in1(A[22]), .out(multiplexer_22_out), .sel(S[0]));
  Multiplexer #(.enable("false")) multiplexer_23 (.in0(A[22]), .in1(A[23]), .out(multiplexer_23_out), .sel(S[0]));
  Multiplexer #(.enable("false")) multiplexer_24 (.in0(A[23]), .in1(A[24]), .out(multiplexer_24_out), .sel(S[0]));
  Multiplexer #(.enable("false")) multiplexer_25 (.in0(A[24]), .in1(A[25]), .out(multiplexer_25_out), .sel(S[0]));
  Multiplexer #(.enable("false")) multiplexer_26 (.in0(A[25]), .in1(A[26]), .out(multiplexer_26_out), .sel(S[0]));
  Multiplexer #(.enable("false")) multiplexer_27 (.in0(A[26]), .in1(A[27]), .out(multiplexer_27_out), .sel(S[0]));
  Multiplexer #(.enable("false")) multiplexer_28 (.in0(A[27]), .in1(A[28]), .out(multiplexer_28_out), .sel(S[0]));
  Multiplexer #(.enable("false")) multiplexer_29 (.in0(A[28]), .in1(A[29]), .out(multiplexer_29_out), .sel(S[0]));
  Multiplexer #(.enable("false")) multiplexer_30 (.in0(A[29]), .in1(A[30]), .out(multiplexer_30_out), .sel(S[0]));
  Multiplexer #(.enable("false")) multiplexer_31 (.in0(A[30]), .in1(A[31]), .out(multiplexer_31_out), .sel(S[0]));
  Multiplexer #(.enable("false")) multiplexer_32 (.in0(A[31]), .in1(Si), .out(multiplexer_32_out), .sel(S[0]));
  Multiplexer #(.enable("false")) multiplexer_33 (
    .in0(multiplexer_1_out), .in1(multiplexer_3_out), .out(multiplexer_33_out), .sel(S[1]));
  Multiplexer #(.enable("false")) multiplexer_34 (
    .in0(multiplexer_2_out), .in1(multiplexer_4_out), .out(multiplexer_34_out), .sel(S[1]));
  Multiplexer #(.enable("false")) multiplexer_35 (
    .in0(multiplexer_3_out), .in1(multiplexer_5_out), .out(multiplexer_35_out), .sel(S[1]));
  Multiplexer #(.enable("false")) multiplexer_36 (
    .in0(multiplexer_4_out), .in1(multiplexer_6_out), .out(multiplexer_36_out), .sel(S[1]));
  Multiplexer #(.enable("false")) multiplexer_37 (
    .in0(multiplexer_5_out), .in1(multiplexer_7_out), .out(multiplexer_37_out), .sel(S[1]));
  Multiplexer #(.enable("false")) multiplexer_38 (
    .in0(multiplexer_6_out), .in1(multiplexer_8_out), .out(multiplexer_38_out), .sel(S[1]));
  Multiplexer #(.enable("false")) multiplexer_39 (
    .in0(multiplexer_7_out), .in1(multiplexer_9_out), .out(multiplexer_39_out), .sel(S[1]));
  Multiplexer #(.enable("false")) multiplexer_40 (
    .in0(multiplexer_8_out), .in1(multiplexer_10_out), .out(multiplexer_40_out), .sel(S[1]));
  Multiplexer #(.enable("false")) multiplexer_41 (
    .in0(multiplexer_9_out), .in1(multiplexer_11_out), .out(multiplexer_41_out), .sel(S[1]));
  Multiplexer #(.enable("false")) multiplexer_42 (
    .in0(multiplexer_10_out), .in1(multiplexer_12_out), .out(multiplexer_42_out), .sel(S[1]));
  Multiplexer #(.enable("false")) multiplexer_43 (
    .in0(multiplexer_11_out), .in1(multiplexer_13_out), .out(multiplexer_43_out), .sel(S[1]));
  Multiplexer #(.enable("false")) multiplexer_44 (
    .in0(multiplexer_12_out), .in1(multiplexer_14_out), .out(multiplexer_44_out), .sel(S[1]));
  Multiplexer #(.enable("false")) multiplexer_45 (
    .in0(multiplexer_13_out), .in1(multiplexer_15_out), .out(multiplexer_45_out), .sel(S[1]));
  Multiplexer #(.enable("false")) multiplexer_46 (
    .in0(multiplexer_14_out), .in1(multiplexer_16_out), .out(multiplexer_46_out), .sel(S[1]));
  Multiplexer #(.enable("false")) multiplexer_47 (
    .in0(multiplexer_15_out), .in1(multiplexer_17_out), .out(multiplexer_47_out), .sel(S[1]));
  Multiplexer #(.enable("false")) multiplexer_48 (
    .in0(multiplexer_16_out), .in1(multiplexer_18_out), .out(multiplexer_48_out), .sel(S[1]));
  Multiplexer #(.enable("false")) multiplexer_49 (
    .in0(multiplexer_17_out), .in1(multiplexer_19_out), .out(multiplexer_49_out), .sel(S[1]));
  Multiplexer #(.enable("false")) multiplexer_50 (
    .in0(multiplexer_18_out), .in1(multiplexer_20_out), .out(multiplexer_50_out), .sel(S[1]));
  Multiplexer #(.enable("false")) multiplexer_51 (
    .in0(multiplexer_19_out), .in1(multiplexer_21_out), .out(multiplexer_51_out), .sel(S[1]));
  Multiplexer #(.enable("false")) multiplexer_52 (
    .in0(multiplexer_20_out), .in1(multiplexer_22_out), .out(multiplexer_52_out), .sel(S[1]));
  Multiplexer #(.enable("false")) multiplexer_53 (
    .in0(multiplexer_21_out), .in1(multiplexer_23_out), .out(multiplexer_53_out), .sel(S[1]));
  Multiplexer #(.enable("false")) multiplexer_54 (
    .in0(multiplexer_22_out), .in1(multiplexer_24_out), .out(multiplexer_54_out), .sel(S[1]));
  Multiplexer #(.enable("false")) multiplexer_55 (
    .in0(multiplexer_23_out), .in1(multiplexer_25_out), .out(multiplexer_55_out), .sel(S[1]));
  Multiplexer #(.enable("false")) multiplexer_56 (
    .in0(multiplexer_24_out), .in1(multiplexer_26_out), .out(multiplexer_56_out), .sel(S[1]));
  Multiplexer #(.enable("false")) multiplexer_57 (
    .in0(multiplexer_25_out), .in1(multiplexer_27_out), .out(multiplexer_57_out), .sel(S[1]));
  Multiplexer #(.enable("false")) multiplexer_58 (
    .in0(multiplexer_26_out), .in1(multiplexer_28_out), .out(multiplexer_58_out), .sel(S[1]));
  Multiplexer #(.enable("false")) multiplexer_59 (
    .in0(multiplexer_27_out), .in1(multiplexer_29_out), .out(multiplexer_59_out), .sel(S[1]));
  Multiplexer #(.enable("false")) multiplexer_60 (
    .in0(multiplexer_28_out), .in1(multiplexer_30_out), .out(multiplexer_60_out), .sel(S[1]));
  Multiplexer #(.enable("false")) multiplexer_61 (
    .in0(multiplexer_29_out), .in1(multiplexer_31_out), .out(multiplexer_61_out), .sel(S[1]));
  Multiplexer #(.enable("false")) multiplexer_62 (
    .in0(multiplexer_30_out), .in1(multiplexer_32_out), .out(multiplexer_62_out), .sel(S[1]));
  Multiplexer #(.enable("false")) multiplexer_63 (
    .in0(multiplexer_31_out), .in1(Si), .out(multiplexer_63_out), .sel(S[1]));
  Multiplexer #(.enable("false")) multiplexer_64 (
    .in0(multiplexer_32_out), .in1(Si), .out(multiplexer_64_out), .sel(S[1]));
  Multiplexer #(.enable("false")) multiplexer_65 (
    .in0(multiplexer_33_out), .in1(multiplexer_37_out), .out(multiplexer_65_out), .sel(S[2]));
  Multiplexer #(.enable("false")) multiplexer_66 (
    .in0(multiplexer_34_out), .in1(multiplexer_38_out), .out(multiplexer_66_out), .sel(S[2]));
  Multiplexer #(.enable("false")) multiplexer_67 (
    .in0(multiplexer_35_out), .in1(multiplexer_39_out), .out(multiplexer_67_out), .sel(S[2]));
  Multiplexer #(.enable("false")) multiplexer_68 (
    .in0(multiplexer_36_out), .in1(multiplexer_40_out), .out(multiplexer_68_out), .sel(S[2]));
  Multiplexer #(.enable("false")) multiplexer_69 (
    .in0(multiplexer_37_out), .in1(multiplexer_41_out), .out(multiplexer_69_out), .sel(S[2]));
  Multiplexer #(.enable("false")) multiplexer_70 (
    .in0(multiplexer_38_out), .in1(multiplexer_42_out), .out(multiplexer_70_out), .sel(S[2]));
  Multiplexer #(.enable("false")) multiplexer_71 (
    .in0(multiplexer_39_out), .in1(multiplexer_43_out), .out(multiplexer_71_out), .sel(S[2]));
  Multiplexer #(.enable("false")) multiplexer_72 (
    .in0(multiplexer_40_out), .in1(multiplexer_44_out), .out(multiplexer_72_out), .sel(S[2]));
  Multiplexer #(.enable("false")) multiplexer_73 (
    .in0(multiplexer_41_out), .in1(multiplexer_45_out), .out(multiplexer_73_out), .sel(S[2]));
  Multiplexer #(.enable("false")) multiplexer_74 (
    .in0(multiplexer_42_out), .in1(multiplexer_46_out), .out(multiplexer_74_out), .sel(S[2]));
  Multiplexer #(.enable("false")) multiplexer_75 (
    .in0(multiplexer_43_out), .in1(multiplexer_47_out), .out(multiplexer_75_out), .sel(S[2]));
  Multiplexer #(.enable("false")) multiplexer_76 (
    .in0(multiplexer_44_out), .in1(multiplexer_48_out), .out(multiplexer_76_out), .sel(S[2]));
  Multiplexer #(.enable("false")) multiplexer_77 (
    .in0(multiplexer_45_out), .in1(multiplexer_49_out), .out(multiplexer_77_out), .sel(S[2]));
  Multiplexer #(.enable("false")) multiplexer_78 (
    .in0(multiplexer_46_out), .in1(multiplexer_50_out), .out(multiplexer_78_out), .sel(S[2]));
  Multiplexer #(.enable("false")) multiplexer_79 (
    .in0(multiplexer_47_out), .in1(multiplexer_51_out), .out(multiplexer_79_out), .sel(S[2]));
  Multiplexer #(.enable("false")) multiplexer_80 (
    .in0(multiplexer_48_out), .in1(multiplexer_52_out), .out(multiplexer_80_out), .sel(S[2]));
  Multiplexer #(.enable("false")) multiplexer_81 (
    .in0(multiplexer_49_out), .in1(multiplexer_53_out), .out(multiplexer_81_out), .sel(S[2]));
  Multiplexer #(.enable("false")) multiplexer_82 (
    .in0(multiplexer_50_out), .in1(multiplexer_54_out), .out(multiplexer_82_out), .sel(S[2]));
  Multiplexer #(.enable("false")) multiplexer_83 (
    .in0(multiplexer_51_out), .in1(multiplexer_55_out), .out(multiplexer_83_out), .sel(S[2]));
  Multiplexer #(.enable("false")) multiplexer_84 (
    .in0(multiplexer_52_out), .in1(multiplexer_56_out), .out(multiplexer_84_out), .sel(S[2]));
  Multiplexer #(.enable("false")) multiplexer_85 (
    .in0(multiplexer_53_out), .in1(multiplexer_57_out), .out(multiplexer_85_out), .sel(S[2]));
  Multiplexer #(.enable("false")) multiplexer_86 (
    .in0(multiplexer_54_out), .in1(multiplexer_58_out), .out(multiplexer_86_out), .sel(S[2]));
  Multiplexer #(.enable("false")) multiplexer_87 (
    .in0(multiplexer_55_out), .in1(multiplexer_59_out), .out(multiplexer_87_out), .sel(S[2]));
  Multiplexer #(.enable("false")) multiplexer_88 (
    .in0(multiplexer_56_out), .in1(multiplexer_60_out), .out(multiplexer_88_out), .sel(S[2]));
  Multiplexer #(.enable("false")) multiplexer_89 (
    .in0(multiplexer_57_out), .in1(multiplexer_61_out), .out(multiplexer_89_out), .sel(S[2]));
  Multiplexer #(.enable("false")) multiplexer_90 (
    .in0(multiplexer_58_out), .in1(multiplexer_62_out), .out(multiplexer_90_out), .sel(S[2]));
  Multiplexer #(.enable("false")) multiplexer_91 (
    .in0(multiplexer_59_out), .in1(multiplexer_63_out), .out(multiplexer_91_out), .sel(S[2]));
  Multiplexer #(.enable("false")) multiplexer_92 (
    .in0(multiplexer_60_out), .in1(multiplexer_64_out), .out(multiplexer_92_out), .sel(S[2]));
  Multiplexer #(.enable("false")) multiplexer_93 (
    .in0(multiplexer_61_out), .in1(Si), .out(multiplexer_93_out), .sel(S[2]));
  Multiplexer #(.enable("false")) multiplexer_94 (
    .in0(multiplexer_62_out), .in1(Si), .out(multiplexer_94_out), .sel(S[2]));
  Multiplexer #(.enable("false")) multiplexer_95 (
    .in0(multiplexer_63_out), .in1(Si), .out(multiplexer_95_out), .sel(S[2]));
  Multiplexer #(.enable("false")) multiplexer_96 (
    .in0(multiplexer_64_out), .in1(Si), .out(multiplexer_96_out), .sel(S[2]));
  Multiplexer #(.enable("false")) multiplexer_97 (
    .in0(multiplexer_65_out), .in1(multiplexer_73_out), .out(multiplexer_97_out), .sel(S[3]));
  Multiplexer #(.enable("false")) multiplexer_98 (
    .in0(multiplexer_66_out), .in1(multiplexer_74_out), .out(multiplexer_98_out), .sel(S[3]));
  Multiplexer #(.enable("false")) multiplexer_99 (
    .in0(multiplexer_67_out), .in1(multiplexer_75_out), .out(multiplexer_99_out), .sel(S[3]));
  Multiplexer #(.enable("false")) multiplexer_100 (
    .in0(multiplexer_68_out), .in1(multiplexer_76_out), .out(multiplexer_100_out), .sel(S[3]));
  Multiplexer #(.enable("false")) multiplexer_101 (
    .in0(multiplexer_69_out), .in1(multiplexer_77_out), .out(multiplexer_101_out), .sel(S[3]));
  Multiplexer #(.enable("false")) multiplexer_102 (
    .in0(multiplexer_70_out), .in1(multiplexer_78_out), .out(multiplexer_102_out), .sel(S[3]));
  Multiplexer #(.enable("false")) multiplexer_103 (
    .in0(multiplexer_71_out), .in1(multiplexer_79_out), .out(multiplexer_103_out), .sel(S[3]));
  Multiplexer #(.enable("false")) multiplexer_104 (
    .in0(multiplexer_72_out), .in1(multiplexer_80_out), .out(multiplexer_104_out), .sel(S[3]));
  Multiplexer #(.enable("false")) multiplexer_105 (
    .in0(multiplexer_73_out), .in1(multiplexer_81_out), .out(multiplexer_105_out), .sel(S[3]));
  Multiplexer #(.enable("false")) multiplexer_106 (
    .in0(multiplexer_74_out), .in1(multiplexer_82_out), .out(multiplexer_106_out), .sel(S[3]));
  Multiplexer #(.enable("false")) multiplexer_107 (
    .in0(multiplexer_75_out), .in1(multiplexer_83_out), .out(multiplexer_107_out), .sel(S[3]));
  Multiplexer #(.enable("false")) multiplexer_108 (
    .in0(multiplexer_76_out), .in1(multiplexer_84_out), .out(multiplexer_108_out), .sel(S[3]));
  Multiplexer #(.enable("false")) multiplexer_109 (
    .in0(multiplexer_77_out), .in1(multiplexer_85_out), .out(multiplexer_109_out), .sel(S[3]));
  Multiplexer #(.enable("false")) multiplexer_110 (
    .in0(multiplexer_78_out), .in1(multiplexer_86_out), .out(multiplexer_110_out), .sel(S[3]));
  Multiplexer #(.enable("false")) multiplexer_111 (
    .in0(multiplexer_79_out), .in1(multiplexer_87_out), .out(multiplexer_111_out), .sel(S[3]));
  Multiplexer #(.enable("false")) multiplexer_112 (
    .in0(multiplexer_80_out), .in1(multiplexer_88_out), .out(multiplexer_112_out), .sel(S[3]));
  Multiplexer #(.enable("false")) multiplexer_113 (
    .in0(multiplexer_81_out), .in1(multiplexer_89_out), .out(multiplexer_113_out), .sel(S[3]));
  Multiplexer #(.enable("false")) multiplexer_114 (
    .in0(multiplexer_82_out), .in1(multiplexer_90_out), .out(multiplexer_114_out), .sel(S[3]));
  Multiplexer #(.enable("false")) multiplexer_115 (
    .in0(multiplexer_83_out), .in1(multiplexer_91_out), .out(multiplexer_115_out), .sel(S[3]));
  Multiplexer #(.enable("false")) multiplexer_116 (
    .in0(multiplexer_84_out), .in1(multiplexer_92_out), .out(multiplexer_116_out), .sel(S[3]));
  Multiplexer #(.enable("false")) multiplexer_117 (
    .in0(multiplexer_85_out), .in1(multiplexer_93_out), .out(multiplexer_117_out), .sel(S[3]));
  Multiplexer #(.enable("false")) multiplexer_118 (
    .in0(multiplexer_86_out), .in1(multiplexer_94_out), .out(multiplexer_118_out), .sel(S[3]));
  Multiplexer #(.enable("false")) multiplexer_119 (
    .in0(multiplexer_87_out), .in1(multiplexer_95_out), .out(multiplexer_119_out), .sel(S[3]));
  Multiplexer #(.enable("false")) multiplexer_120 (
    .in0(multiplexer_88_out), .in1(multiplexer_96_out), .out(multiplexer_120_out), .sel(S[3]));
  Multiplexer #(.enable("false")) multiplexer_121 (
    .in0(multiplexer_89_out), .in1(Si), .out(multiplexer_121_out), .sel(S[3]));
  Multiplexer #(.enable("false")) multiplexer_122 (
    .in0(multiplexer_90_out), .in1(Si), .out(multiplexer_122_out), .sel(S[3]));
  Multiplexer #(.enable("false")) multiplexer_123 (
    .in0(multiplexer_91_out), .in1(Si), .out(multiplexer_123_out), .sel(S[3]));
  Multiplexer #(.enable("false")) multiplexer_124 (
    .in0(multiplexer_92_out), .in1(Si), .out(multiplexer_124_out), .sel(S[3]));
  Multiplexer #(.enable("false")) multiplexer_125 (
    .in0(multiplexer_93_out), .in1(Si), .out(multiplexer_125_out), .sel(S[3]));
  Multiplexer #(.enable("false")) multiplexer_126 (
    .in0(multiplexer_94_out), .in1(Si), .out(multiplexer_126_out), .sel(S[3]));
  Multiplexer #(.enable("false")) multiplexer_127 (
    .in0(multiplexer_95_out), .in1(Si), .out(multiplexer_127_out), .sel(S[3]));
  Multiplexer #(.enable("false")) multiplexer_128 (
    .in0(multiplexer_96_out), .in1(Si), .out(multiplexer_128_out), .sel(S[3]));
  Multiplexer #(.enable("false")) multiplexer_129 (
    .in0(multiplexer_97_out), .in1(multiplexer_113_out), .out(R[0]), .sel(S[4]));
  Multiplexer #(.enable("false")) multiplexer_130 (
    .in0(multiplexer_98_out), .in1(multiplexer_114_out), .out(R[1]), .sel(S[4]));
  Multiplexer #(.enable("false")) multiplexer_131 (
    .in0(multiplexer_99_out), .in1(multiplexer_115_out), .out(R[2]), .sel(S[4]));
  Multiplexer #(.enable("false")) multiplexer_132 (
    .in0(multiplexer_100_out), .in1(multiplexer_116_out), .out(R[3]), .sel(S[4]));
  Multiplexer #(.enable("false")) multiplexer_133 (
    .in0(multiplexer_101_out), .in1(multiplexer_117_out), .out(R[4]), .sel(S[4]));
  Multiplexer #(.enable("false")) multiplexer_134 (
    .in0(multiplexer_102_out), .in1(multiplexer_118_out), .out(R[5]), .sel(S[4]));
  Multiplexer #(.enable("false")) multiplexer_135 (
    .in0(multiplexer_103_out), .in1(multiplexer_119_out), .out(R[6]), .sel(S[4]));
  Multiplexer #(.enable("false")) multiplexer_136 (
    .in0(multiplexer_104_out), .in1(multiplexer_120_out), .out(R[7]), .sel(S[4]));
  Multiplexer #(.enable("false")) multiplexer_137 (
    .in0(multiplexer_105_out), .in1(multiplexer_121_out), .out(R[8]), .sel(S[4]));
  Multiplexer #(.enable("false")) multiplexer_138 (
    .in0(multiplexer_106_out), .in1(multiplexer_122_out), .out(R[9]), .sel(S[4]));
  Multiplexer #(.enable("false")) multiplexer_139 (
    .in0(multiplexer_107_out), .in1(multiplexer_123_out), .out(R[10]), .sel(S[4]));
  Multiplexer #(.enable("false")) multiplexer_140 (
    .in0(multiplexer_108_out), .in1(multiplexer_124_out), .out(R[11]), .sel(S[4]));
  Multiplexer #(.enable("false")) multiplexer_141 (
    .in0(multiplexer_109_out), .in1(multiplexer_125_out), .out(R[12]), .sel(S[4]));
  Multiplexer #(.enable("false")) multiplexer_142 (
    .in0(multiplexer_110_out), .in1(multiplexer_126_out), .out(R[13]), .sel(S[4]));
  Multiplexer #(.enable("false")) multiplexer_143 (
    .in0(multiplexer_111_out), .in1(multiplexer_127_out), .out(R[14]), .sel(S[4]));
  Multiplexer #(.enable("false")) multiplexer_144 (
    .in0(multiplexer_112_out), .in1(multiplexer_128_out), .out(R[15]), .sel(S[4]));
  Multiplexer #(.enable("false")) multiplexer_145 (.in0(multiplexer_113_out), .in1(Si), .out(R[16]), .sel(S[4]));
  Multiplexer #(.enable("false")) multiplexer_146 (.in0(multiplexer_114_out), .in1(Si), .out(R[17]), .sel(S[4]));
  Multiplexer #(.enable("false")) multiplexer_147 (.in0(multiplexer_115_out), .in1(Si), .out(R[18]), .sel(S[4]));
  Multiplexer #(.enable("false")) multiplexer_148 (.in0(multiplexer_116_out), .in1(Si), .out(R[19]), .sel(S[4]));
  Multiplexer #(.enable("false")) multiplexer_149 (.in0(multiplexer_117_out), .in1(Si), .out(R[20]), .sel(S[4]));
  Multiplexer #(.enable("false")) multiplexer_150 (.in0(multiplexer_118_out), .in1(Si), .out(R[21]), .sel(S[4]));
  Multiplexer #(.enable("false")) multiplexer_151 (.in0(multiplexer_119_out), .in1(Si), .out(R[22]), .sel(S[4]));
  Multiplexer #(.enable("false")) multiplexer_152 (.in0(multiplexer_120_out), .in1(Si), .out(R[23]), .sel(S[4]));
  Multiplexer #(.enable("false")) multiplexer_153 (.in0(multiplexer_121_out), .in1(Si), .out(R[24]), .sel(S[4]));
  Multiplexer #(.enable("false")) multiplexer_154 (.in0(multiplexer_122_out), .in1(Si), .out(R[25]), .sel(S[4]));
  Multiplexer #(.enable("false")) multiplexer_155 (.in0(multiplexer_123_out), .in1(Si), .out(R[26]), .sel(S[4]));
  Multiplexer #(.enable("false")) multiplexer_156 (.in0(multiplexer_124_out), .in1(Si), .out(R[27]), .sel(S[4]));
  Multiplexer #(.enable("false")) multiplexer_157 (.in0(multiplexer_125_out), .in1(Si), .out(R[28]), .sel(S[4]));
  Multiplexer #(.enable("false")) multiplexer_158 (.in0(multiplexer_126_out), .in1(Si), .out(R[29]), .sel(S[4]));
  Multiplexer #(.enable("false")) multiplexer_159 (.in0(multiplexer_127_out), .in1(Si), .out(R[30]), .sel(S[4]));
  Multiplexer #(.enable("false")) multiplexer_160 (.in0(multiplexer_128_out), .in1(Si), .out(R[31]), .sel(S[4]));
endmodule

module LShifter (
  input  S0,
  input  Si,
  input  [31:0] A,
  output [31:0] R
);

  Multiplexer #(.enable("false")) multiplexer_1 (.in0(A[0]), .in1(Si), .out(R[0]), .sel(S0));
  Multiplexer #(.enable("false")) multiplexer_2 (.in0(A[1]), .in1(A[0]), .out(R[1]), .sel(S0));
  Multiplexer #(.enable("false")) multiplexer_3 (.in0(A[2]), .in1(A[1]), .out(R[2]), .sel(S0));
  Multiplexer #(.enable("false")) multiplexer_4 (.in0(A[3]), .in1(A[2]), .out(R[3]), .sel(S0));
  Multiplexer #(.enable("false")) multiplexer_5 (.in0(A[4]), .in1(A[3]), .out(R[4]), .sel(S0));
  Multiplexer #(.enable("false")) multiplexer_6 (.in0(A[5]), .in1(A[4]), .out(R[5]), .sel(S0));
  Multiplexer #(.enable("false")) multiplexer_7 (.in0(A[6]), .in1(A[5]), .out(R[6]), .sel(S0));
  Multiplexer #(.enable("false")) multiplexer_8 (.in0(A[7]), .in1(A[6]), .out(R[7]), .sel(S0));
  Multiplexer #(.enable("false")) multiplexer_9 (.in0(A[8]), .in1(A[7]), .out(R[8]), .sel(S0));
  Multiplexer #(.enable("false")) multiplexer_10 (.in0(A[9]), .in1(A[8]), .out(R[9]), .sel(S0));
  Multiplexer #(.enable("false")) multiplexer_11 (.in0(A[10]), .in1(A[9]), .out(R[10]), .sel(S0));
  Multiplexer #(.enable("false")) multiplexer_12 (.in0(A[11]), .in1(A[10]), .out(R[11]), .sel(S0));
  Multiplexer #(.enable("false")) multiplexer_13 (.in0(A[12]), .in1(A[11]), .out(R[12]), .sel(S0));
  Multiplexer #(.enable("false")) multiplexer_14 (.in0(A[13]), .in1(A[12]), .out(R[13]), .sel(S0));
  Multiplexer #(.enable("false")) multiplexer_15 (.in0(A[14]), .in1(A[13]), .out(R[14]), .sel(S0));
  Multiplexer #(.enable("false")) multiplexer_16 (.in0(A[15]), .in1(A[14]), .out(R[15]), .sel(S0));
  Multiplexer #(.enable("false")) multiplexer_17 (.in0(A[16]), .in1(A[15]), .out(R[16]), .sel(S0));
  Multiplexer #(.enable("false")) multiplexer_18 (.in0(A[17]), .in1(A[16]), .out(R[17]), .sel(S0));
  Multiplexer #(.enable("false")) multiplexer_19 (.in0(A[18]), .in1(A[17]), .out(R[18]), .sel(S0));
  Multiplexer #(.enable("false")) multiplexer_20 (.in0(A[19]), .in1(A[18]), .out(R[19]), .sel(S0));
  Multiplexer #(.enable("false")) multiplexer_21 (.in0(A[20]), .in1(A[19]), .out(R[20]), .sel(S0));
  Multiplexer #(.enable("false")) multiplexer_22 (.in0(A[21]), .in1(A[20]), .out(R[21]), .sel(S0));
  Multiplexer #(.enable("false")) multiplexer_23 (.in0(A[22]), .in1(A[21]), .out(R[22]), .sel(S0));
  Multiplexer #(.enable("false")) multiplexer_24 (.in0(A[23]), .in1(A[22]), .out(R[23]), .sel(S0));
  Multiplexer #(.enable("false")) multiplexer_25 (.in0(A[24]), .in1(A[23]), .out(R[24]), .sel(S0));
  Multiplexer #(.enable("false")) multiplexer_26 (.in0(A[25]), .in1(A[24]), .out(R[25]), .sel(S0));
  Multiplexer #(.enable("false")) multiplexer_27 (.in0(A[26]), .in1(A[25]), .out(R[26]), .sel(S0));
  Multiplexer #(.enable("false")) multiplexer_28 (.in0(A[27]), .in1(A[26]), .out(R[27]), .sel(S0));
  Multiplexer #(.enable("false")) multiplexer_29 (.in0(A[28]), .in1(A[27]), .out(R[28]), .sel(S0));
  Multiplexer #(.enable("false")) multiplexer_30 (.in0(A[29]), .in1(A[28]), .out(R[29]), .sel(S0));
  Multiplexer #(.enable("false")) multiplexer_31 (.in0(A[30]), .in1(A[29]), .out(R[30]), .sel(S0));
  Multiplexer #(.enable("false")) multiplexer_32 (.in0(A[31]), .in1(A[30]), .out(R[31]), .sel(S0));
endmodule

module FLShifter (
  input  [4:0] S,
  input  Si,
  input  [31:0] A,
  output [31:0] R
);

  wire multiplexer_1_out, multiplexer_2_out, multiplexer_3_out, multiplexer_4_out, multiplexer_5_out,
       multiplexer_6_out, multiplexer_7_out, multiplexer_8_out, multiplexer_9_out, multiplexer_10_out,
       multiplexer_11_out, multiplexer_12_out, multiplexer_13_out, multiplexer_14_out, multiplexer_15_out,
       multiplexer_16_out, multiplexer_17_out, multiplexer_18_out, multiplexer_19_out, multiplexer_20_out,
       multiplexer_21_out, multiplexer_22_out, multiplexer_23_out, multiplexer_24_out, multiplexer_25_out,
       multiplexer_26_out, multiplexer_27_out, multiplexer_28_out, multiplexer_29_out, multiplexer_30_out,
       multiplexer_31_out, multiplexer_32_out, multiplexer_33_out, multiplexer_34_out, multiplexer_35_out,
       multiplexer_36_out, multiplexer_37_out, multiplexer_38_out, multiplexer_39_out, multiplexer_40_out,
       multiplexer_41_out, multiplexer_42_out, multiplexer_43_out, multiplexer_44_out, multiplexer_45_out,
       multiplexer_46_out, multiplexer_47_out, multiplexer_48_out, multiplexer_49_out, multiplexer_50_out,
       multiplexer_51_out, multiplexer_52_out, multiplexer_53_out, multiplexer_54_out, multiplexer_55_out,
       multiplexer_56_out, multiplexer_57_out, multiplexer_58_out, multiplexer_59_out, multiplexer_60_out,
       multiplexer_61_out, multiplexer_62_out, multiplexer_63_out, multiplexer_64_out, multiplexer_65_out,
       multiplexer_66_out, multiplexer_67_out, multiplexer_68_out, multiplexer_69_out, multiplexer_70_out,
       multiplexer_71_out, multiplexer_72_out, multiplexer_73_out, multiplexer_74_out, multiplexer_75_out,
       multiplexer_76_out, multiplexer_77_out, multiplexer_78_out, multiplexer_79_out, multiplexer_80_out,
       multiplexer_81_out, multiplexer_82_out, multiplexer_83_out, multiplexer_84_out, multiplexer_85_out,
       multiplexer_86_out, multiplexer_87_out, multiplexer_88_out, multiplexer_89_out, multiplexer_90_out,
       multiplexer_91_out, multiplexer_92_out, multiplexer_93_out, multiplexer_94_out, multiplexer_95_out,
       multiplexer_96_out, multiplexer_97_out, multiplexer_98_out, multiplexer_99_out, multiplexer_100_out,
       multiplexer_101_out, multiplexer_102_out, multiplexer_103_out, multiplexer_104_out,
       multiplexer_105_out, multiplexer_106_out, multiplexer_107_out, multiplexer_108_out,
       multiplexer_109_out, multiplexer_110_out, multiplexer_111_out, multiplexer_112_out,
       multiplexer_114_out, multiplexer_115_out, multiplexer_116_out, multiplexer_117_out,
       multiplexer_118_out, multiplexer_119_out, multiplexer_120_out, multiplexer_121_out,
       multiplexer_122_out, multiplexer_123_out, multiplexer_124_out, multiplexer_125_out,
       multiplexer_126_out, multiplexer_127_out, multiplexer_128_out;

  Multiplexer #(.enable("false")) multiplexer_1 (.in0(A[0]), .in1(Si), .out(multiplexer_1_out), .sel(S[0]));
  Multiplexer #(.enable("false")) multiplexer_2 (.in0(A[1]), .in1(A[0]), .out(multiplexer_2_out), .sel(S[0]));
  Multiplexer #(.enable("false")) multiplexer_3 (.in0(A[2]), .in1(A[1]), .out(multiplexer_3_out), .sel(S[0]));
  Multiplexer #(.enable("false")) multiplexer_4 (.in0(A[3]), .in1(A[2]), .out(multiplexer_4_out), .sel(S[0]));
  Multiplexer #(.enable("false")) multiplexer_5 (.in0(A[4]), .in1(A[3]), .out(multiplexer_5_out), .sel(S[0]));
  Multiplexer #(.enable("false")) multiplexer_6 (.in0(A[5]), .in1(A[4]), .out(multiplexer_6_out), .sel(S[0]));
  Multiplexer #(.enable("false")) multiplexer_7 (.in0(A[6]), .in1(A[5]), .out(multiplexer_7_out), .sel(S[0]));
  Multiplexer #(.enable("false")) multiplexer_8 (.in0(A[7]), .in1(A[6]), .out(multiplexer_8_out), .sel(S[0]));
  Multiplexer #(.enable("false")) multiplexer_9 (.in0(A[8]), .in1(A[7]), .out(multiplexer_9_out), .sel(S[0]));
  Multiplexer #(.enable("false")) multiplexer_10 (.in0(A[9]), .in1(A[8]), .out(multiplexer_10_out), .sel(S[0]));
  Multiplexer #(.enable("false")) multiplexer_11 (.in0(A[10]), .in1(A[9]), .out(multiplexer_11_out), .sel(S[0]));
  Multiplexer #(.enable("false")) multiplexer_12 (.in0(A[11]), .in1(A[10]), .out(multiplexer_12_out), .sel(S[0]));
  Multiplexer #(.enable("false")) multiplexer_13 (.in0(A[12]), .in1(A[11]), .out(multiplexer_13_out), .sel(S[0]));
  Multiplexer #(.enable("false")) multiplexer_14 (.in0(A[13]), .in1(A[12]), .out(multiplexer_14_out), .sel(S[0]));
  Multiplexer #(.enable("false")) multiplexer_15 (.in0(A[14]), .in1(A[13]), .out(multiplexer_15_out), .sel(S[0]));
  Multiplexer #(.enable("false")) multiplexer_16 (.in0(A[15]), .in1(A[14]), .out(multiplexer_16_out), .sel(S[0]));
  Multiplexer #(.enable("false")) multiplexer_17 (.in0(A[16]), .in1(A[15]), .out(multiplexer_17_out), .sel(S[0]));
  Multiplexer #(.enable("false")) multiplexer_18 (.in0(A[17]), .in1(A[16]), .out(multiplexer_18_out), .sel(S[0]));
  Multiplexer #(.enable("false")) multiplexer_19 (.in0(A[18]), .in1(A[17]), .out(multiplexer_19_out), .sel(S[0]));
  Multiplexer #(.enable("false")) multiplexer_20 (.in0(A[19]), .in1(A[18]), .out(multiplexer_20_out), .sel(S[0]));
  Multiplexer #(.enable("false")) multiplexer_21 (.in0(A[20]), .in1(A[19]), .out(multiplexer_21_out), .sel(S[0]));
  Multiplexer #(.enable("false")) multiplexer_22 (.in0(A[21]), .in1(A[20]), .out(multiplexer_22_out), .sel(S[0]));
  Multiplexer #(.enable("false")) multiplexer_23 (.in0(A[22]), .in1(A[21]), .out(multiplexer_23_out), .sel(S[0]));
  Multiplexer #(.enable("false")) multiplexer_24 (.in0(A[23]), .in1(A[22]), .out(multiplexer_24_out), .sel(S[0]));
  Multiplexer #(.enable("false")) multiplexer_25 (.in0(A[24]), .in1(A[23]), .out(multiplexer_25_out), .sel(S[0]));
  Multiplexer #(.enable("false")) multiplexer_26 (.in0(A[25]), .in1(A[24]), .out(multiplexer_26_out), .sel(S[0]));
  Multiplexer #(.enable("false")) multiplexer_27 (.in0(A[26]), .in1(A[25]), .out(multiplexer_27_out), .sel(S[0]));
  Multiplexer #(.enable("false")) multiplexer_28 (.in0(A[27]), .in1(A[26]), .out(multiplexer_28_out), .sel(S[0]));
  Multiplexer #(.enable("false")) multiplexer_29 (.in0(A[28]), .in1(A[27]), .out(multiplexer_29_out), .sel(S[0]));
  Multiplexer #(.enable("false")) multiplexer_30 (.in0(A[29]), .in1(A[28]), .out(multiplexer_30_out), .sel(S[0]));
  Multiplexer #(.enable("false")) multiplexer_31 (.in0(A[30]), .in1(A[29]), .out(multiplexer_31_out), .sel(S[0]));
  Multiplexer #(.enable("false")) multiplexer_32 (.in0(A[31]), .in1(A[30]), .out(multiplexer_32_out), .sel(S[0]));
  Multiplexer #(.enable("false")) multiplexer_33 (
    .in0(multiplexer_1_out), .in1(Si), .out(multiplexer_33_out), .sel(S[1]));
  Multiplexer #(.enable("false")) multiplexer_34 (
    .in0(multiplexer_2_out), .in1(Si), .out(multiplexer_34_out), .sel(S[1]));
  Multiplexer #(.enable("false")) multiplexer_35 (
    .in0(multiplexer_3_out), .in1(multiplexer_1_out), .out(multiplexer_35_out), .sel(S[1]));
  Multiplexer #(.enable("false")) multiplexer_36 (
    .in0(multiplexer_4_out), .in1(multiplexer_2_out), .out(multiplexer_36_out), .sel(S[1]));
  Multiplexer #(.enable("false")) multiplexer_37 (
    .in0(multiplexer_5_out), .in1(multiplexer_3_out), .out(multiplexer_37_out), .sel(S[1]));
  Multiplexer #(.enable("false")) multiplexer_38 (
    .in0(multiplexer_6_out), .in1(multiplexer_4_out), .out(multiplexer_38_out), .sel(S[1]));
  Multiplexer #(.enable("false")) multiplexer_39 (
    .in0(multiplexer_7_out), .in1(multiplexer_5_out), .out(multiplexer_39_out), .sel(S[1]));
  Multiplexer #(.enable("false")) multiplexer_40 (
    .in0(multiplexer_8_out), .in1(multiplexer_6_out), .out(multiplexer_40_out), .sel(S[1]));
  Multiplexer #(.enable("false")) multiplexer_41 (
    .in0(multiplexer_9_out), .in1(multiplexer_7_out), .out(multiplexer_41_out), .sel(S[1]));
  Multiplexer #(.enable("false")) multiplexer_42 (
    .in0(multiplexer_10_out), .in1(multiplexer_8_out), .out(multiplexer_42_out), .sel(S[1]));
  Multiplexer #(.enable("false")) multiplexer_43 (
    .in0(multiplexer_11_out), .in1(multiplexer_9_out), .out(multiplexer_43_out), .sel(S[1]));
  Multiplexer #(.enable("false")) multiplexer_44 (
    .in0(multiplexer_12_out), .in1(multiplexer_10_out), .out(multiplexer_44_out), .sel(S[1]));
  Multiplexer #(.enable("false")) multiplexer_45 (
    .in0(multiplexer_13_out), .in1(multiplexer_11_out), .out(multiplexer_45_out), .sel(S[1]));
  Multiplexer #(.enable("false")) multiplexer_46 (
    .in0(multiplexer_14_out), .in1(multiplexer_12_out), .out(multiplexer_46_out), .sel(S[1]));
  Multiplexer #(.enable("false")) multiplexer_47 (
    .in0(multiplexer_15_out), .in1(multiplexer_13_out), .out(multiplexer_47_out), .sel(S[1]));
  Multiplexer #(.enable("false")) multiplexer_48 (
    .in0(multiplexer_16_out), .in1(multiplexer_14_out), .out(multiplexer_48_out), .sel(S[1]));
  Multiplexer #(.enable("false")) multiplexer_49 (
    .in0(multiplexer_17_out), .in1(multiplexer_15_out), .out(multiplexer_49_out), .sel(S[1]));
  Multiplexer #(.enable("false")) multiplexer_50 (
    .in0(multiplexer_18_out), .in1(multiplexer_16_out), .out(multiplexer_50_out), .sel(S[1]));
  Multiplexer #(.enable("false")) multiplexer_51 (
    .in0(multiplexer_19_out), .in1(multiplexer_17_out), .out(multiplexer_51_out), .sel(S[1]));
  Multiplexer #(.enable("false")) multiplexer_52 (
    .in0(multiplexer_20_out), .in1(multiplexer_18_out), .out(multiplexer_52_out), .sel(S[1]));
  Multiplexer #(.enable("false")) multiplexer_53 (
    .in0(multiplexer_21_out), .in1(multiplexer_19_out), .out(multiplexer_53_out), .sel(S[1]));
  Multiplexer #(.enable("false")) multiplexer_54 (
    .in0(multiplexer_22_out), .in1(multiplexer_20_out), .out(multiplexer_54_out), .sel(S[1]));
  Multiplexer #(.enable("false")) multiplexer_55 (
    .in0(multiplexer_23_out), .in1(multiplexer_21_out), .out(multiplexer_55_out), .sel(S[1]));
  Multiplexer #(.enable("false")) multiplexer_56 (
    .in0(multiplexer_24_out), .in1(multiplexer_22_out), .out(multiplexer_56_out), .sel(S[1]));
  Multiplexer #(.enable("false")) multiplexer_57 (
    .in0(multiplexer_25_out), .in1(multiplexer_23_out), .out(multiplexer_57_out), .sel(S[1]));
  Multiplexer #(.enable("false")) multiplexer_58 (
    .in0(multiplexer_26_out), .in1(multiplexer_24_out), .out(multiplexer_58_out), .sel(S[1]));
  Multiplexer #(.enable("false")) multiplexer_59 (
    .in0(multiplexer_27_out), .in1(multiplexer_25_out), .out(multiplexer_59_out), .sel(S[1]));
  Multiplexer #(.enable("false")) multiplexer_60 (
    .in0(multiplexer_28_out), .in1(multiplexer_26_out), .out(multiplexer_60_out), .sel(S[1]));
  Multiplexer #(.enable("false")) multiplexer_61 (
    .in0(multiplexer_29_out), .in1(multiplexer_27_out), .out(multiplexer_61_out), .sel(S[1]));
  Multiplexer #(.enable("false")) multiplexer_62 (
    .in0(multiplexer_30_out), .in1(multiplexer_28_out), .out(multiplexer_62_out), .sel(S[1]));
  Multiplexer #(.enable("false")) multiplexer_63 (
    .in0(multiplexer_31_out), .in1(multiplexer_29_out), .out(multiplexer_63_out), .sel(S[1]));
  Multiplexer #(.enable("false")) multiplexer_64 (
    .in0(multiplexer_32_out), .in1(multiplexer_30_out), .out(multiplexer_64_out), .sel(S[1]));
  Multiplexer #(.enable("false")) multiplexer_65 (
    .in0(multiplexer_33_out), .in1(Si), .out(multiplexer_65_out), .sel(S[2]));
  Multiplexer #(.enable("false")) multiplexer_66 (
    .in0(multiplexer_34_out), .in1(Si), .out(multiplexer_66_out), .sel(S[2]));
  Multiplexer #(.enable("false")) multiplexer_67 (
    .in0(multiplexer_35_out), .in1(Si), .out(multiplexer_67_out), .sel(S[2]));
  Multiplexer #(.enable("false")) multiplexer_68 (
    .in0(multiplexer_36_out), .in1(Si), .out(multiplexer_68_out), .sel(S[2]));
  Multiplexer #(.enable("false")) multiplexer_69 (
    .in0(multiplexer_37_out), .in1(multiplexer_33_out), .out(multiplexer_69_out), .sel(S[2]));
  Multiplexer #(.enable("false")) multiplexer_70 (
    .in0(multiplexer_38_out), .in1(multiplexer_34_out), .out(multiplexer_70_out), .sel(S[2]));
  Multiplexer #(.enable("false")) multiplexer_71 (
    .in0(multiplexer_39_out), .in1(multiplexer_35_out), .out(multiplexer_71_out), .sel(S[2]));
  Multiplexer #(.enable("false")) multiplexer_72 (
    .in0(multiplexer_40_out), .in1(multiplexer_36_out), .out(multiplexer_72_out), .sel(S[2]));
  Multiplexer #(.enable("false")) multiplexer_73 (
    .in0(multiplexer_41_out), .in1(multiplexer_37_out), .out(multiplexer_73_out), .sel(S[2]));
  Multiplexer #(.enable("false")) multiplexer_74 (
    .in0(multiplexer_42_out), .in1(multiplexer_38_out), .out(multiplexer_74_out), .sel(S[2]));
  Multiplexer #(.enable("false")) multiplexer_75 (
    .in0(multiplexer_43_out), .in1(multiplexer_39_out), .out(multiplexer_75_out), .sel(S[2]));
  Multiplexer #(.enable("false")) multiplexer_76 (
    .in0(multiplexer_44_out), .in1(multiplexer_40_out), .out(multiplexer_76_out), .sel(S[2]));
  Multiplexer #(.enable("false")) multiplexer_77 (
    .in0(multiplexer_45_out), .in1(multiplexer_41_out), .out(multiplexer_77_out), .sel(S[2]));
  Multiplexer #(.enable("false")) multiplexer_78 (
    .in0(multiplexer_46_out), .in1(multiplexer_42_out), .out(multiplexer_78_out), .sel(S[2]));
  Multiplexer #(.enable("false")) multiplexer_79 (
    .in0(multiplexer_47_out), .in1(multiplexer_43_out), .out(multiplexer_79_out), .sel(S[2]));
  Multiplexer #(.enable("false")) multiplexer_80 (
    .in0(multiplexer_48_out), .in1(multiplexer_44_out), .out(multiplexer_80_out), .sel(S[2]));
  Multiplexer #(.enable("false")) multiplexer_81 (
    .in0(multiplexer_49_out), .in1(multiplexer_45_out), .out(multiplexer_81_out), .sel(S[2]));
  Multiplexer #(.enable("false")) multiplexer_82 (
    .in0(multiplexer_50_out), .in1(multiplexer_46_out), .out(multiplexer_82_out), .sel(S[2]));
  Multiplexer #(.enable("false")) multiplexer_83 (
    .in0(multiplexer_51_out), .in1(multiplexer_47_out), .out(multiplexer_83_out), .sel(S[2]));
  Multiplexer #(.enable("false")) multiplexer_84 (
    .in0(multiplexer_52_out), .in1(multiplexer_48_out), .out(multiplexer_84_out), .sel(S[2]));
  Multiplexer #(.enable("false")) multiplexer_85 (
    .in0(multiplexer_53_out), .in1(multiplexer_49_out), .out(multiplexer_85_out), .sel(S[2]));
  Multiplexer #(.enable("false")) multiplexer_86 (
    .in0(multiplexer_54_out), .in1(multiplexer_50_out), .out(multiplexer_86_out), .sel(S[2]));
  Multiplexer #(.enable("false")) multiplexer_87 (
    .in0(multiplexer_55_out), .in1(multiplexer_51_out), .out(multiplexer_87_out), .sel(S[2]));
  Multiplexer #(.enable("false")) multiplexer_88 (
    .in0(multiplexer_56_out), .in1(multiplexer_52_out), .out(multiplexer_88_out), .sel(S[2]));
  Multiplexer #(.enable("false")) multiplexer_89 (
    .in0(multiplexer_57_out), .in1(multiplexer_53_out), .out(multiplexer_89_out), .sel(S[2]));
  Multiplexer #(.enable("false")) multiplexer_90 (
    .in0(multiplexer_58_out), .in1(multiplexer_54_out), .out(multiplexer_90_out), .sel(S[2]));
  Multiplexer #(.enable("false")) multiplexer_91 (
    .in0(multiplexer_59_out), .in1(multiplexer_55_out), .out(multiplexer_91_out), .sel(S[2]));
  Multiplexer #(.enable("false")) multiplexer_92 (
    .in0(multiplexer_60_out), .in1(multiplexer_56_out), .out(multiplexer_92_out), .sel(S[2]));
  Multiplexer #(.enable("false")) multiplexer_93 (
    .in0(multiplexer_61_out), .in1(multiplexer_57_out), .out(multiplexer_93_out), .sel(S[2]));
  Multiplexer #(.enable("false")) multiplexer_94 (
    .in0(multiplexer_62_out), .in1(multiplexer_58_out), .out(multiplexer_94_out), .sel(S[2]));
  Multiplexer #(.enable("false")) multiplexer_95 (
    .in0(multiplexer_63_out), .in1(multiplexer_59_out), .out(multiplexer_95_out), .sel(S[2]));
  Multiplexer #(.enable("false")) multiplexer_96 (
    .in0(multiplexer_64_out), .in1(multiplexer_60_out), .out(multiplexer_96_out), .sel(S[2]));
  Multiplexer #(.enable("false")) multiplexer_97 (
    .in0(multiplexer_65_out), .in1(Si), .out(multiplexer_97_out), .sel(S[3]));
  Multiplexer #(.enable("false")) multiplexer_98 (
    .in0(multiplexer_66_out), .in1(Si), .out(multiplexer_98_out), .sel(S[3]));
  Multiplexer #(.enable("false")) multiplexer_99 (
    .in0(multiplexer_67_out), .in1(Si), .out(multiplexer_99_out), .sel(S[3]));
  Multiplexer #(.enable("false")) multiplexer_100 (
    .in0(multiplexer_68_out), .in1(Si), .out(multiplexer_100_out), .sel(S[3]));
  Multiplexer #(.enable("false")) multiplexer_101 (
    .in0(multiplexer_69_out), .in1(Si), .out(multiplexer_101_out), .sel(S[3]));
  Multiplexer #(.enable("false")) multiplexer_102 (
    .in0(multiplexer_70_out), .in1(Si), .out(multiplexer_102_out), .sel(S[3]));
  Multiplexer #(.enable("false")) multiplexer_103 (
    .in0(multiplexer_71_out), .in1(Si), .out(multiplexer_103_out), .sel(S[3]));
  Multiplexer #(.enable("false")) multiplexer_104 (
    .in0(multiplexer_72_out), .in1(Si), .out(multiplexer_104_out), .sel(S[3]));
  Multiplexer #(.enable("false")) multiplexer_105 (
    .in0(multiplexer_73_out), .in1(multiplexer_65_out), .out(multiplexer_105_out), .sel(S[3]));
  Multiplexer #(.enable("false")) multiplexer_106 (
    .in0(multiplexer_74_out), .in1(multiplexer_66_out), .out(multiplexer_106_out), .sel(S[3]));
  Multiplexer #(.enable("false")) multiplexer_107 (
    .in0(multiplexer_75_out), .in1(multiplexer_67_out), .out(multiplexer_107_out), .sel(S[3]));
  Multiplexer #(.enable("false")) multiplexer_108 (
    .in0(multiplexer_76_out), .in1(multiplexer_68_out), .out(multiplexer_108_out), .sel(S[3]));
  Multiplexer #(.enable("false")) multiplexer_109 (
    .in0(multiplexer_77_out), .in1(multiplexer_69_out), .out(multiplexer_109_out), .sel(S[3]));
  Multiplexer #(.enable("false")) multiplexer_110 (
    .in0(multiplexer_78_out), .in1(multiplexer_70_out), .out(multiplexer_110_out), .sel(S[3]));
  Multiplexer #(.enable("false")) multiplexer_111 (
    .in0(multiplexer_79_out), .in1(multiplexer_71_out), .out(multiplexer_111_out), .sel(S[3]));
  Multiplexer #(.enable("false")) multiplexer_112 (
    .in0(multiplexer_80_out), .in1(multiplexer_72_out), .out(multiplexer_112_out), .sel(S[3]));
  Multiplexer #(.enable("false")) multiplexer_113 (
    .in0(multiplexer_81_out), .in1(multiplexer_73_out), .sel(S[3]));  // open: out
  Multiplexer #(.enable("false")) multiplexer_114 (
    .in0(multiplexer_82_out), .in1(multiplexer_74_out), .out(multiplexer_114_out), .sel(S[3]));
  Multiplexer #(.enable("false")) multiplexer_115 (
    .in0(multiplexer_83_out), .in1(multiplexer_75_out), .out(multiplexer_115_out), .sel(S[3]));
  Multiplexer #(.enable("false")) multiplexer_116 (
    .in0(multiplexer_84_out), .in1(multiplexer_76_out), .out(multiplexer_116_out), .sel(S[3]));
  Multiplexer #(.enable("false")) multiplexer_117 (
    .in0(multiplexer_85_out), .in1(multiplexer_77_out), .out(multiplexer_117_out), .sel(S[3]));
  Multiplexer #(.enable("false")) multiplexer_118 (
    .in0(multiplexer_86_out), .in1(multiplexer_78_out), .out(multiplexer_118_out), .sel(S[3]));
  Multiplexer #(.enable("false")) multiplexer_119 (
    .in0(multiplexer_87_out), .in1(multiplexer_79_out), .out(multiplexer_119_out), .sel(S[3]));
  Multiplexer #(.enable("false")) multiplexer_120 (
    .in0(multiplexer_88_out), .in1(multiplexer_80_out), .out(multiplexer_120_out), .sel(S[3]));
  Multiplexer #(.enable("false")) multiplexer_121 (
    .in0(multiplexer_89_out), .in1(multiplexer_81_out), .out(multiplexer_121_out), .sel(S[3]));
  Multiplexer #(.enable("false")) multiplexer_122 (
    .in0(multiplexer_90_out), .in1(multiplexer_82_out), .out(multiplexer_122_out), .sel(S[3]));
  Multiplexer #(.enable("false")) multiplexer_123 (
    .in0(multiplexer_91_out), .in1(multiplexer_83_out), .out(multiplexer_123_out), .sel(S[3]));
  Multiplexer #(.enable("false")) multiplexer_124 (
    .in0(multiplexer_92_out), .in1(multiplexer_84_out), .out(multiplexer_124_out), .sel(S[3]));
  Multiplexer #(.enable("false")) multiplexer_125 (
    .in0(multiplexer_93_out), .in1(multiplexer_85_out), .out(multiplexer_125_out), .sel(S[3]));
  Multiplexer #(.enable("false")) multiplexer_126 (
    .in0(multiplexer_94_out), .in1(multiplexer_86_out), .out(multiplexer_126_out), .sel(S[3]));
  Multiplexer #(.enable("false")) multiplexer_127 (
    .in0(multiplexer_95_out), .in1(multiplexer_87_out), .out(multiplexer_127_out), .sel(S[3]));
  Multiplexer #(.enable("false")) multiplexer_128 (
    .in0(multiplexer_96_out), .in1(multiplexer_88_out), .out(multiplexer_128_out), .sel(S[3]));
  Multiplexer #(.enable("false")) multiplexer_129 (.in0(multiplexer_97_out), .in1(Si), .out(R[0]), .sel(S[4]));
  Multiplexer #(.enable("false")) multiplexer_130 (.in0(multiplexer_98_out), .in1(Si), .out(R[1]), .sel(S[4]));
  Multiplexer #(.enable("false")) multiplexer_131 (.in0(multiplexer_99_out), .in1(Si), .out(R[2]), .sel(S[4]));
  Multiplexer #(.enable("false")) multiplexer_132 (.in0(multiplexer_100_out), .in1(Si), .out(R[3]), .sel(S[4]));
  Multiplexer #(.enable("false")) multiplexer_133 (.in0(multiplexer_101_out), .in1(Si), .out(R[4]), .sel(S[4]));
  Multiplexer #(.enable("false")) multiplexer_134 (.in0(multiplexer_102_out), .in1(Si), .out(R[5]), .sel(S[4]));
  Multiplexer #(.enable("false")) multiplexer_135 (.in0(multiplexer_103_out), .in1(Si), .out(R[6]), .sel(S[4]));
  Multiplexer #(.enable("false")) multiplexer_136 (.in0(multiplexer_104_out), .in1(Si), .out(R[7]), .sel(S[4]));
  Multiplexer #(.enable("false")) multiplexer_137 (.in0(multiplexer_105_out), .in1(Si), .out(R[8]), .sel(S[4]));
  Multiplexer #(.enable("false")) multiplexer_138 (.in0(multiplexer_106_out), .in1(Si), .out(R[9]), .sel(S[4]));
  Multiplexer #(.enable("false")) multiplexer_139 (.in0(multiplexer_107_out), .in1(Si), .out(R[10]), .sel(S[4]));
  Multiplexer #(.enable("false")) multiplexer_140 (.in0(multiplexer_108_out), .in1(Si), .out(R[11]), .sel(S[4]));
  Multiplexer #(.enable("false")) multiplexer_141 (.in0(multiplexer_109_out), .in1(Si), .out(R[12]), .sel(S[4]));
  Multiplexer #(.enable("false")) multiplexer_142 (.in0(multiplexer_110_out), .in1(Si), .out(R[13]), .sel(S[4]));
  Multiplexer #(.enable("false")) multiplexer_143 (.in0(multiplexer_111_out), .in1(Si), .out(R[14]), .sel(S[4]));
  Multiplexer #(.enable("false")) multiplexer_144 (.in0(multiplexer_112_out), .in1(Si), .out(R[15]), .sel(S[4]));
  Multiplexer #(.enable("false")) multiplexer_145 (.in0(S[4]), .in1(multiplexer_97_out), .out(R[16]), .sel(S[4]));
  Multiplexer #(.enable("false")) multiplexer_146 (
    .in0(multiplexer_114_out), .in1(multiplexer_98_out), .out(R[17]), .sel(S[4]));
  Multiplexer #(.enable("false")) multiplexer_147 (
    .in0(multiplexer_115_out), .in1(multiplexer_99_out), .out(R[18]), .sel(S[4]));
  Multiplexer #(.enable("false")) multiplexer_148 (
    .in0(multiplexer_116_out), .in1(multiplexer_100_out), .out(R[19]), .sel(S[4]));
  Multiplexer #(.enable("false")) multiplexer_149 (
    .in0(multiplexer_117_out), .in1(multiplexer_101_out), .out(R[20]), .sel(S[4]));
  Multiplexer #(.enable("false")) multiplexer_150 (
    .in0(multiplexer_118_out), .in1(multiplexer_102_out), .out(R[21]), .sel(S[4]));
  Multiplexer #(.enable("false")) multiplexer_151 (
    .in0(multiplexer_119_out), .in1(multiplexer_103_out), .out(R[22]), .sel(S[4]));
  Multiplexer #(.enable("false")) multiplexer_152 (
    .in0(multiplexer_120_out), .in1(multiplexer_104_out), .out(R[23]), .sel(S[4]));
  Multiplexer #(.enable("false")) multiplexer_153 (
    .in0(multiplexer_121_out), .in1(multiplexer_105_out), .out(R[24]), .sel(S[4]));
  Multiplexer #(.enable("false")) multiplexer_154 (
    .in0(multiplexer_122_out), .in1(multiplexer_106_out), .out(R[25]), .sel(S[4]));
  Multiplexer #(.enable("false")) multiplexer_155 (
    .in0(multiplexer_123_out), .in1(multiplexer_107_out), .out(R[26]), .sel(S[4]));
  Multiplexer #(.enable("false")) multiplexer_156 (
    .in0(multiplexer_124_out), .in1(multiplexer_108_out), .out(R[27]), .sel(S[4]));
  Multiplexer #(.enable("false")) multiplexer_157 (
    .in0(multiplexer_125_out), .in1(multiplexer_109_out), .out(R[28]), .sel(S[4]));
  Multiplexer #(.enable("false")) multiplexer_158 (
    .in0(multiplexer_126_out), .in1(multiplexer_110_out), .out(R[29]), .sel(S[4]));
  Multiplexer #(.enable("false")) multiplexer_159 (
    .in0(multiplexer_127_out), .in1(multiplexer_111_out), .out(R[30]), .sel(S[4]));
  Multiplexer #(.enable("false")) multiplexer_160 (
    .in0(multiplexer_128_out), .in1(multiplexer_112_out), .out(R[31]), .sel(S[4]));
endmodule

module MyShifter (
  input  [4:0] in_1,
  input  in_2,
  input  [31:0] A,
  input  LR,
  output [31:0] R
);

  wire [31:0] flshifter_1_r, frshifter_1_r;

  FRShifter frshifter_1 (.S(in_1), .A(A), .Si(in_2), .R(frshifter_1_r));
  FLShifter flshifter_1 (.S(in_1), .Si(in_2), .A(A), .R(flshifter_1_r));
  Multiplexer #(.width(32), .enable("false")) multiplexer_1 (
    .in0(frshifter_1_r), .in1(flshifter_1_r), .out(R), .sel(LR));
endmodule

module OneMult (
  input  [31:0] A,
  input  [31:0] P,
  input  B0,
  output [31:0] Po,
  output [31:0] Ao
);

  wire [31:0] thirtytwobitadder_1_r;

  LShifter lshifter_1 (.S0(1'b1), .Si(1'b0), .A(A), .R(Po));
  ThirtyTwoBitAdder thirtytwobitadder_1 (.A(A), .B(P), .R(thirtytwobitadder_1_r));  // open: Ci, Co
  Multiplexer #(.width(32), .enable("false")) multiplexer_1 (.in0(P), .in1(thirtytwobitadder_1_r), .out(Ao), .sel(B0));
endmodule

module Mult (
  input  [31:0] A,
  input  [31:0] B,
  output [31:0] R
);

  wire [31:0] m0_ao, m0_po, m1_ao, m1_po, m2_ao, m2_po, m3_ao, m3_po, m4_ao, m4_po, m5_ao, m5_po, m6_ao,
       m6_po, m7_ao, m7_po, m8_ao, m8_po, m9_ao, m9_po, m10_ao, m10_po, m11_ao, m11_po, m12_ao, m12_po,
       m13_ao, m13_po, m14_ao, m14_po, m15_ao, m15_po, m16_ao, m16_po, m17_ao, m17_po, m18_ao, m18_po,
       m19_ao, m19_po, m20_ao, m20_po, m21_ao, m21_po, m22_ao, m22_po, m23_ao, m23_po, m24_ao, m24_po,
       m25_ao, m25_po, m26_ao, m26_po, m27_ao, m27_po, m28_ao, m28_po, m29_ao, m29_po, m30_ao, m30_po;

  OneMult m0 (.Ao(m0_ao), .B0(B[0]), .A(A), .Po(m0_po));  // open: P
  OneMult m1 (.Ao(m1_ao), .B0(B[1]), .A(m0_po), .P(m0_ao), .Po(m1_po));
  OneMult m2 (.Ao(m2_ao), .B0(B[2]), .A(m1_po), .P(m1_ao), .Po(m2_po));
  OneMult m3 (.Ao(m3_ao), .B0(B[3]), .A(m2_po), .P(m2_ao), .Po(m3_po));
  OneMult m4 (.Ao(m4_ao), .B0(B[4]), .A(m3_po), .P(m3_ao), .Po(m4_po));
  OneMult m5 (.Ao(m5_ao), .B0(B[5]), .A(m4_po), .P(m4_ao), .Po(m5_po));
  OneMult m6 (.Ao(m6_ao), .B0(B[6]), .A(m5_po), .P(m5_ao), .Po(m6_po));
  OneMult m7 (.Ao(m7_ao), .B0(B[7]), .A(m6_po), .P(m6_ao), .Po(m7_po));
  OneMult m8 (.Ao(m8_ao), .B0(B[8]), .A(m7_po), .P(m7_ao), .Po(m8_po));
  OneMult m9 (.Ao(m9_ao), .B0(B[9]), .A(m8_po), .P(m8_ao), .Po(m9_po));
  OneMult m10 (.Ao(m10_ao), .B0(B[10]), .A(m9_po), .P(m9_ao), .Po(m10_po));
  OneMult m11 (.Ao(m11_ao), .B0(B[11]), .A(m10_po), .P(m10_ao), .Po(m11_po));
  OneMult m12 (.Ao(m12_ao), .B0(B[12]), .A(m11_po), .P(m11_ao), .Po(m12_po));
  OneMult m13 (.Ao(m13_ao), .B0(B[13]), .A(m12_po), .P(m12_ao), .Po(m13_po));
  OneMult m14 (.Ao(m14_ao), .B0(B[14]), .A(m13_po), .P(m13_ao), .Po(m14_po));
  OneMult m15 (.Ao(m15_ao), .B0(B[15]), .A(m14_po), .P(m14_ao), .Po(m15_po));
  OneMult m16 (.Ao(m16_ao), .B0(B[16]), .A(m15_po), .P(m15_ao), .Po(m16_po));
  OneMult m17 (.Ao(m17_ao), .B0(B[17]), .A(m16_po), .P(m16_ao), .Po(m17_po));
  OneMult m18 (.Ao(m18_ao), .B0(B[18]), .A(m17_po), .P(m17_ao), .Po(m18_po));
  OneMult m19 (.Ao(m19_ao), .B0(B[19]), .A(m18_po), .P(m18_ao), .Po(m19_po));
  OneMult m20 (.Ao(m20_ao), .B0(B[20]), .A(m19_po), .P(m19_ao), .Po(m20_po));
  OneMult m21 (.Ao(m21_ao), .B0(B[21]), .A(m20_po), .P(m20_ao), .Po(m21_po));
  OneMult m22 (.Ao(m22_ao), .B0(B[22]), .A(m21_po), .P(m21_ao), .Po(m22_po));
  OneMult m23 (.Ao(m23_ao), .B0(B[23]), .A(m22_po), .P(m22_ao), .Po(m23_po));
  OneMult m24 (.Ao(m24_ao), .B0(B[24]), .A(m23_po), .P(m23_ao), .Po(m24_po));
  OneMult m25 (.Ao(m25_ao), .B0(B[25]), .A(m24_po), .P(m24_ao), .Po(m25_po));
  OneMult m26 (.Ao(m26_ao), .B0(B[26]), .A(m25_po), .P(m25_ao), .Po(m26_po));
  OneMult m27 (.Ao(m27_ao), .B0(B[27]), .A(m26_po), .P(m26_ao), .Po(m27_po));
  OneMult m28 (.Ao(m28_ao), .B0(B[28]), .A(m27_po), .P(m27_ao), .Po(m28_po));
  OneMult m29 (.Ao(m29_ao), .B0(B[29]), .A(m28_po), .P(m28_ao), .Po(m29_po));
  OneMult m30 (.Ao(m30_ao), .B0(B[30]), .A(m29_po), .P(m29_ao), .Po(m30_po));
  OneMult m31 (.Ao(R), .B0(B[31]), .A(m30_po), .P(m30_ao));  // open: Po
endmodule

module OneDiv (
  input  [31:0] Remainder,
  input  [31:0] Divisor,
  input  [31:0] InDividend,
  input  [31:0] Quotient,
  output [31:0] Remainder2,
  output [31:0] Divisor2,
  output [31:0] InDiv2,
  output [31:0] Quotient2
);

  wire not_1_out, thirtytwobitsubstraction_1_alessthanb;
  wire [31:0] lshifter_1_r, thirtytwobitsubstraction_1_r;

  not not_1 (not_1_out, thirtytwobitsubstraction_1_alessthanb);
  LShifter lshifter_1 (.S0(1'b1), .Si(InDividend[31]), .A(Remainder), .R(lshifter_1_r));
  ThirtyTwoBitSubstraction thirtytwobitsubstraction_1 (
    .A(lshifter_1_r), .B(Divisor), .R(thirtytwobitsubstraction_1_r),
    .ALessThanB(thirtytwobitsubstraction_1_alessthanb));
  Multiplexer #(.width(32), .enable("false")) multiplexer_1 (
    .in0(thirtytwobitsubstraction_1_r), .in1(Remainder), .out(Remainder2), .sel(not_1_out));
  LShifter lshifter_2 (.S0(1'b1), .Si(1'b0), .A(InDividend), .R(InDiv2));
  LShifter lshifter_3 (.S0(1'b1), .Si(thirtytwobitsubstraction_1_alessthanb), .A(Quotient), .R(Quotient2));

  assign Divisor2 = Divisor;
endmodule

module Div (
  input  [31:0] in_1,
  input  [31:0] Divisor,
  input  [31:0] Dividend,
  input  [31:0] in_4,
  output [31:0] out_5,
  output [31:0] out_6,
  output [31:0] out_7,
  output [31:0] out_8
);

  wire [31:0] onediv_1_divisor2, onediv_1_indiv2, onediv_1_quotient2, onediv_1_remainder2, onediv_2_divisor2,
       onediv_2_indiv2, onediv_2_quotient2, onediv_2_remainder2, onediv_3_divisor2, onediv_3_indiv2,
       onediv_3_quotient2, onediv_3_remainder2, onediv_4_divisor2, onediv_4_indiv2, onediv_4_quotient2,
       onediv_4_remainder2, onediv_5_divisor2, onediv_5_indiv2, onediv_5_quotient2, onediv_5_remainder2,
       onediv_6_divisor2, onediv_6_indiv2, onediv_6_quotient2, onediv_6_remainder2, onediv_7_divisor2,
       onediv_7_indiv2, onediv_7_quotient2, onediv_7_remainder2, onediv_8_divisor2, onediv_8_indiv2,
       onediv_8_quotient2, onediv_8_remainder2, onediv_9_divisor2, onediv_9_indiv2, onediv_9_quotient2,
       onediv_9_remainder2, onediv_10_divisor2, onediv_10_indiv2, onediv_10_quotient2, onediv_10_remainder2,
       onediv_11_divisor2, onediv_11_indiv2, onediv_11_quotient2, onediv_11_remainder2, onediv_12_divisor2,
       onediv_12_indiv2, onediv_12_quotient2, onediv_12_remainder2, onediv_13_divisor2, onediv_13_indiv2,
       onediv_13_quotient2, onediv_13_remainder2, onediv_14_divisor2, onediv_14_indiv2, onediv_14_quotient2,
       onediv_14_remainder2, onediv_15_divisor2, onediv_15_indiv2, onediv_15_quotient2, onediv_15_remainder2,
       onediv_16_divisor2, onediv_16_indiv2, onediv_16_quotient2, onediv_16_remainder2, onediv_17_divisor2,
       onediv_17_indiv2, onediv_17_quotient2, onediv_17_remainder2, onediv_18_divisor2, onediv_18_indiv2,
       onediv_18_quotient2, onediv_18_remainder2, onediv_19_divisor2, onediv_19_indiv2, onediv_19_quotient2,
       onediv_19_remainder2, onediv_20_divisor2, onediv_20_indiv2, onediv_20_quotient2, onediv_20_remainder2,
       onediv_21_divisor2, onediv_21_indiv2, onediv_21_quotient2, onediv_21_remainder2, onediv_22_divisor2,
       onediv_22_indiv2, onediv_22_quotient2, onediv_22_remainder2, onediv_23_divisor2, onediv_23_indiv2,
       onediv_23_quotient2, onediv_23_remainder2, onediv_24_divisor2, onediv_24_indiv2, onediv_24_quotient2,
       onediv_24_remainder2, onediv_25_divisor2, onediv_25_indiv2, onediv_25_quotient2, onediv_25_remainder2,
       onediv_26_divisor2, onediv_26_indiv2, onediv_26_quotient2, onediv_26_remainder2, onediv_27_divisor2,
       onediv_27_indiv2, onediv_27_quotient2, onediv_27_remainder2, onediv_28_divisor2, onediv_28_indiv2,
       onediv_28_quotient2, onediv_28_remainder2, onediv_29_divisor2, onediv_29_indiv2, onediv_29_quotient2,
       onediv_29_remainder2, onediv_30_divisor2, onediv_30_indiv2, onediv_30_quotient2, onediv_30_remainder2,
       onediv_31_divisor2, onediv_31_indiv2, onediv_31_quotient2, onediv_31_remainder2;

  OneDiv onediv_1 (
    .Remainder(in_1), .Divisor(Divisor), .InDividend(Dividend), .Quotient(in_4),
    .Remainder2(onediv_1_remainder2), .Divisor2(onediv_1_divisor2), .InDiv2(onediv_1_indiv2),
    .Quotient2(onediv_1_quotient2));
  OneDiv onediv_2 (
    .Remainder(onediv_1_remainder2), .Divisor(onediv_1_divisor2), .InDividend(onediv_1_indiv2),
    .Quotient(onediv_1_quotient2), .Remainder2(onediv_2_remainder2), .Divisor2(onediv_2_divisor2),
    .InDiv2(onediv_2_indiv2), .Quotient2(onediv_2_quotient2));
  OneDiv onediv_3 (
    .Remainder(onediv_2_remainder2), .Divisor(onediv_2_divisor2), .InDividend(onediv_2_indiv2),
    .Quotient(onediv_2_quotient2), .Remainder2(onediv_3_remainder2), .Divisor2(onediv_3_divisor2),
    .InDiv2(onediv_3_indiv2), .Quotient2(onediv_3_quotient2));
  OneDiv onediv_4 (
    .Remainder(onediv_3_remainder2), .Divisor(onediv_3_divisor2), .InDividend(onediv_3_indiv2),
    .Quotient(onediv_3_quotient2), .Remainder2(onediv_4_remainder2), .Divisor2(onediv_4_divisor2),
    .InDiv2(onediv_4_indiv2), .Quotient2(onediv_4_quotient2));
  OneDiv onediv_5 (
    .Remainder(onediv_4_remainder2), .Divisor(onediv_4_divisor2), .InDividend(onediv_4_indiv2),
    .Quotient(onediv_4_quotient2), .Remainder2(onediv_5_remainder2), .Divisor2(onediv_5_divisor2),
    .InDiv2(onediv_5_indiv2), .Quotient2(onediv_5_quotient2));
  OneDiv onediv_6 (
    .Remainder(onediv_5_remainder2), .Divisor(onediv_5_divisor2), .InDividend(onediv_5_indiv2),
    .Quotient(onediv_5_quotient2), .Remainder2(onediv_6_remainder2), .Divisor2(onediv_6_divisor2),
    .InDiv2(onediv_6_indiv2), .Quotient2(onediv_6_quotient2));
  OneDiv onediv_7 (
    .Remainder(onediv_6_remainder2), .Divisor(onediv_6_divisor2), .InDividend(onediv_6_indiv2),
    .Quotient(onediv_6_quotient2), .Remainder2(onediv_7_remainder2), .Divisor2(onediv_7_divisor2),
    .InDiv2(onediv_7_indiv2), .Quotient2(onediv_7_quotient2));
  OneDiv onediv_8 (
    .Remainder(onediv_7_remainder2), .Divisor(onediv_7_divisor2), .InDividend(onediv_7_indiv2),
    .Quotient(onediv_7_quotient2), .Remainder2(onediv_8_remainder2), .Divisor2(onediv_8_divisor2),
    .InDiv2(onediv_8_indiv2), .Quotient2(onediv_8_quotient2));
  OneDiv onediv_9 (
    .Remainder(onediv_8_remainder2), .Divisor(onediv_8_divisor2), .InDividend(onediv_8_indiv2),
    .Quotient(onediv_8_quotient2), .Remainder2(onediv_9_remainder2), .Divisor2(onediv_9_divisor2),
    .InDiv2(onediv_9_indiv2), .Quotient2(onediv_9_quotient2));
  OneDiv onediv_10 (
    .Remainder(onediv_9_remainder2), .Divisor(onediv_9_divisor2), .InDividend(onediv_9_indiv2),
    .Quotient(onediv_9_quotient2), .Remainder2(onediv_10_remainder2), .Divisor2(onediv_10_divisor2),
    .InDiv2(onediv_10_indiv2), .Quotient2(onediv_10_quotient2));
  OneDiv onediv_11 (
    .Remainder(onediv_10_remainder2), .Divisor(onediv_10_divisor2), .InDividend(onediv_10_indiv2),
    .Quotient(onediv_10_quotient2), .Remainder2(onediv_11_remainder2), .Divisor2(onediv_11_divisor2),
    .InDiv2(onediv_11_indiv2), .Quotient2(onediv_11_quotient2));
  OneDiv onediv_12 (
    .Remainder(onediv_11_remainder2), .Divisor(onediv_11_divisor2), .InDividend(onediv_11_indiv2),
    .Quotient(onediv_11_quotient2), .Remainder2(onediv_12_remainder2), .Divisor2(onediv_12_divisor2),
    .InDiv2(onediv_12_indiv2), .Quotient2(onediv_12_quotient2));
  OneDiv onediv_13 (
    .Remainder(onediv_12_remainder2), .Divisor(onediv_12_divisor2), .InDividend(onediv_12_indiv2),
    .Quotient(onediv_12_quotient2), .Remainder2(onediv_13_remainder2), .Divisor2(onediv_13_divisor2),
    .InDiv2(onediv_13_indiv2), .Quotient2(onediv_13_quotient2));
  OneDiv onediv_14 (
    .Remainder(onediv_13_remainder2), .Divisor(onediv_13_divisor2), .InDividend(onediv_13_indiv2),
    .Quotient(onediv_13_quotient2), .Remainder2(onediv_14_remainder2), .Divisor2(onediv_14_divisor2),
    .InDiv2(onediv_14_indiv2), .Quotient2(onediv_14_quotient2));
  OneDiv onediv_15 (
    .Remainder(onediv_14_remainder2), .Divisor(onediv_14_divisor2), .InDividend(onediv_14_indiv2),
    .Quotient(onediv_14_quotient2), .Remainder2(onediv_15_remainder2), .Divisor2(onediv_15_divisor2),
    .InDiv2(onediv_15_indiv2), .Quotient2(onediv_15_quotient2));
  OneDiv onediv_16 (
    .Remainder(onediv_15_remainder2), .Divisor(onediv_15_divisor2), .InDividend(onediv_15_indiv2),
    .Quotient(onediv_15_quotient2), .Remainder2(onediv_16_remainder2), .Divisor2(onediv_16_divisor2),
    .InDiv2(onediv_16_indiv2), .Quotient2(onediv_16_quotient2));
  OneDiv onediv_17 (
    .Remainder(onediv_16_remainder2), .Divisor(onediv_16_divisor2), .InDividend(onediv_16_indiv2),
    .Quotient(onediv_16_quotient2), .Remainder2(onediv_17_remainder2), .Divisor2(onediv_17_divisor2),
    .InDiv2(onediv_17_indiv2), .Quotient2(onediv_17_quotient2));
  OneDiv onediv_18 (
    .Remainder(onediv_17_remainder2), .Divisor(onediv_17_divisor2), .InDividend(onediv_17_indiv2),
    .Quotient(onediv_17_quotient2), .Remainder2(onediv_18_remainder2), .Divisor2(onediv_18_divisor2),
    .InDiv2(onediv_18_indiv2), .Quotient2(onediv_18_quotient2));
  OneDiv onediv_19 (
    .Remainder(onediv_18_remainder2), .Divisor(onediv_18_divisor2), .InDividend(onediv_18_indiv2),
    .Quotient(onediv_18_quotient2), .Remainder2(onediv_19_remainder2), .Divisor2(onediv_19_divisor2),
    .InDiv2(onediv_19_indiv2), .Quotient2(onediv_19_quotient2));
  OneDiv onediv_20 (
    .Remainder(onediv_19_remainder2), .Divisor(onediv_19_divisor2), .InDividend(onediv_19_indiv2),
    .Quotient(onediv_19_quotient2), .Remainder2(onediv_20_remainder2), .Divisor2(onediv_20_divisor2),
    .InDiv2(onediv_20_indiv2), .Quotient2(onediv_20_quotient2));
  OneDiv onediv_21 (
    .Remainder(onediv_20_remainder2), .Divisor(onediv_20_divisor2), .InDividend(onediv_20_indiv2),
    .Quotient(onediv_20_quotient2), .Remainder2(onediv_21_remainder2), .Divisor2(onediv_21_divisor2),
    .InDiv2(onediv_21_indiv2), .Quotient2(onediv_21_quotient2));
  OneDiv onediv_22 (
    .Remainder(onediv_21_remainder2), .Divisor(onediv_21_divisor2), .InDividend(onediv_21_indiv2),
    .Quotient(onediv_21_quotient2), .Remainder2(onediv_22_remainder2), .Divisor2(onediv_22_divisor2),
    .InDiv2(onediv_22_indiv2), .Quotient2(onediv_22_quotient2));
  OneDiv onediv_23 (
    .Remainder(onediv_22_remainder2), .Divisor(onediv_22_divisor2), .InDividend(onediv_22_indiv2),
    .Quotient(onediv_22_quotient2), .Remainder2(onediv_23_remainder2), .Divisor2(onediv_23_divisor2),
    .InDiv2(onediv_23_indiv2), .Quotient2(onediv_23_quotient2));
  OneDiv onediv_24 (
    .Remainder(onediv_23_remainder2), .Divisor(onediv_23_divisor2), .InDividend(onediv_23_indiv2),
    .Quotient(onediv_23_quotient2), .Remainder2(onediv_24_remainder2), .Divisor2(onediv_24_divisor2),
    .InDiv2(onediv_24_indiv2), .Quotient2(onediv_24_quotient2));
  OneDiv onediv_25 (
    .Remainder(onediv_24_remainder2), .Divisor(onediv_24_divisor2), .InDividend(onediv_24_indiv2),
    .Quotient(onediv_24_quotient2), .Remainder2(onediv_25_remainder2), .Divisor2(onediv_25_divisor2),
    .InDiv2(onediv_25_indiv2), .Quotient2(onediv_25_quotient2));
  OneDiv onediv_26 (
    .Remainder(onediv_25_remainder2), .Divisor(onediv_25_divisor2), .InDividend(onediv_25_indiv2),
    .Quotient(onediv_25_quotient2), .Remainder2(onediv_26_remainder2), .Divisor2(onediv_26_divisor2),
    .InDiv2(onediv_26_indiv2), .Quotient2(onediv_26_quotient2));
  OneDiv onediv_27 (
    .Remainder(onediv_26_remainder2), .Divisor(onediv_26_divisor2), .InDividend(onediv_26_indiv2),
    .Quotient(onediv_26_quotient2), .Remainder2(onediv_27_remainder2), .Divisor2(onediv_27_divisor2),
    .InDiv2(onediv_27_indiv2), .Quotient2(onediv_27_quotient2));
  OneDiv onediv_28 (
    .Remainder(onediv_27_remainder2), .Divisor(onediv_27_divisor2), .InDividend(onediv_27_indiv2),
    .Quotient(onediv_27_quotient2), .Remainder2(onediv_28_remainder2), .Divisor2(onediv_28_divisor2),
    .InDiv2(onediv_28_indiv2), .Quotient2(onediv_28_quotient2));
  OneDiv onediv_29 (
    .Remainder(onediv_28_remainder2), .Divisor(onediv_28_divisor2), .InDividend(onediv_28_indiv2),
    .Quotient(onediv_28_quotient2), .Remainder2(onediv_29_remainder2), .Divisor2(onediv_29_divisor2),
    .InDiv2(onediv_29_indiv2), .Quotient2(onediv_29_quotient2));
  OneDiv onediv_30 (
    .Remainder(onediv_29_remainder2), .Divisor(onediv_29_divisor2), .InDividend(onediv_29_indiv2),
    .Quotient(onediv_29_quotient2), .Remainder2(onediv_30_remainder2), .Divisor2(onediv_30_divisor2),
    .InDiv2(onediv_30_indiv2), .Quotient2(onediv_30_quotient2));
  OneDiv onediv_31 (
    .Remainder(onediv_30_remainder2), .Divisor(onediv_30_divisor2), .InDividend(onediv_30_indiv2),
    .Quotient(onediv_30_quotient2), .Remainder2(onediv_31_remainder2), .Divisor2(onediv_31_divisor2),
    .InDiv2(onediv_31_indiv2), .Quotient2(onediv_31_quotient2));
  OneDiv onediv_32 (
    .Remainder(onediv_31_remainder2), .Divisor(onediv_31_divisor2), .InDividend(onediv_31_indiv2),
    .Quotient(onediv_31_quotient2), .Remainder2(out_5), .Divisor2(out_6), .InDiv2(out_7), .Quotient2(out_8));
endmodule

module Comp (
  input  [31:0] A,
  input  [31:0] B,
  output [31:0] BEQ,
  output [31:0] BNE,
  output [31:0] BGT,
  output [31:0] BLT
);

  wire and_1_out, and_2_out, nor_1_out, not_1_out, not_2_out, thirtytwobitsubstraction_1_alessthanb;
  wire [31:0] thirtytwobitsubstraction_1_r;

  ThirtyTwoBitSubstraction thirtytwobitsubstraction_1 (
    .A(A), .B(B), .R(thirtytwobitsubstraction_1_r), .ALessThanB(thirtytwobitsubstraction_1_alessthanb));
  nor nor_1 (nor_1_out, thirtytwobitsubstraction_1_r[0], thirtytwobitsubstraction_1_r[1], thirtytwobitsubstraction_1_r[2], thirtytwobitsubstraction_1_r[3], thirtytwobitsubstraction_1_r[4], thirtytwobitsubstraction_1_r[5], thirtytwobitsubstraction_1_r[6], thirtytwobitsubstraction_1_r[7], thirtytwobitsubstraction_1_r[8], thirtytwobitsubstraction_1_r[9], thirtytwobitsubstraction_1_r[10], thirtytwobitsubstraction_1_r[11], thirtytwobitsubstraction_1_r[12], thirtytwobitsubstraction_1_r[13], thirtytwobitsubstraction_1_r[14], thirtytwobitsubstraction_1_r[15], thirtytwobitsubstraction_1_r[16], thirtytwobitsubstraction_1_r[17], thirtytwobitsubstraction_1_r[18], thirtytwobitsubstraction_1_r[19], thirtytwobitsubstraction_1_r[20], thirtytwobitsubstraction_1_r[21], thirtytwobitsubstraction_1_r[22], thirtytwobitsubstraction_1_r[23], thirtytwobitsubstraction_1_r[24], thirtytwobitsubstraction_1_r[25], thirtytwobitsubstraction_1_r[26], thirtytwobitsubstraction_1_r[27], thirtytwobitsubstraction_1_r[28], thirtytwobitsubstraction_1_r[29], thirtytwobitsubstraction_1_r[30], thirtytwobitsubstraction_1_r[31]);
  not not_1 (not_1_out, nor_1_out);
  and and_1 (and_1_out, thirtytwobitsubstraction_1_alessthanb, not_1_out);
  not not_2 (not_2_out, and_1_out);
  and and_2 (and_2_out, not_2_out, not_1_out);
  assign BEQ = {{31{1'b0}}, nor_1_out};  // Bit_Extender bit_extender_1
  assign BNE = {{31{1'b0}}, not_1_out};  // Bit_Extender bit_extender_2
  assign BGT = {{31{1'b0}}, and_1_out};  // Bit_Extender bit_extender_3
  assign BLT = {{31{1'b0}}, and_2_out};  // Bit_Extender bit_extender_4
endmodule

module ALU (
  input  [31:0] A,
  input  [31:0] B,
  input  [4:0] OPPCODE,
  input  [4:0] S,
  input  Sign,
  output [31:0] R
);

  wire [31:0] and_1_out, comp_1_beq, comp_1_bgt, comp_1_blt, comp_1_bne, divider_1_out, flshifter_1_r,
       frshifter_1_r, multiplier_1_out, or_1_out, thirtytwobitadder_1_r, thirtytwobitsubstraction_1_r;

  Multiplier #(.width(32)) multiplier_1 (.a(A), .b(B), .out(multiplier_1_out));  // open: cin, cout
  Divider #(.width(32)) divider_1 (.a(A), .b(B), .out(divider_1_out));  // open: upper, rem
  assign and_1_out = A & B;  // AND_Gate and_1, 32 bits wide
  assign or_1_out = A | B;  // OR_Gate or_1, 32 bits wide
  FLShifter flshifter_1 (.S(S), .Si(Sign), .A(A), .R(flshifter_1_r));
  FRShifter frshifter_1 (.S(S), .A(A), .Si(Sign), .R(frshifter_1_r));
  Comp comp_1 (.A(A), .B(B), .BEQ(comp_1_beq), .BNE(comp_1_bne), .BGT(comp_1_bgt), .BLT(comp_1_blt));
  ThirtyTwoBitAdder thirtytwobitadder_1 (.A(A), .B(B), .R(thirtytwobitadder_1_r));  // open: Ci, Co
  ThirtyTwoBitSubstraction thirtytwobitsubstraction_1 (
    .A(A), .B(B), .R(thirtytwobitsubstraction_1_r));  // open: ALessThanB
  Multiplexer #(.select(5), .width(32), .enable("false")) multiplexer_1 (
    .in0({32{1'b0}}), .in1(thirtytwobitadder_1_r), .in2(thirtytwobitadder_1_r),
    .in3(thirtytwobitsubstraction_1_r), .in4(multiplier_1_out), .in5(divider_1_out), .in6(A), .in7(A),
    .in8(and_1_out), .in9(or_1_out), .in10(flshifter_1_r), .in11(frshifter_1_r), .in12(B), .in13(B),
    .in14(B), .in15(comp_1_beq), .in16(comp_1_bne), .in17(comp_1_bgt), .in18(comp_1_blt), .in19(B), .in20(B),
    .in21(B), .in22(B), .in23(B), .out(R), .sel(OPPCODE));  // open: in24, in25, in26, in27, in28, in29, in30, in31

  // Notes on the sheet:
  //   Juan Jose Elgueta
  //   Abner Xocop
  //   NOTA: El divisior que hicimos no es el que esta aca porque da "Oscillation Apparent" en teoria deberia estar bien pero no lo puedo debuggear
  //   NOTA2: Las comparaciones devuelven 1 si se cumple la condicion o 0 sino en el bit menos significativo de la respuesta
  //   NOTA3: las inputs S y Sign sirven para los shifters, S es la cantidad de corrimientos que se quieren y Sign pushea 1 o 0 a esas posiciones
  //   00000 = ZERO
  //   00001 = ADD
  //   00010 = ADDI
  //   00011 = SUB
  //   00100 =MULT
  //   00111 = MFHO
  //   01000 = AND
  //   01001 = OR
  //   01010 = SLL
  //   01011 = SRL
  //   01100 = J
  //   01101 = JAL
  //   01110 = JR
  //   01111 = BEQ
  //   10000 = BNE
  //   10001 = BGT
  //   10010 = BLT
  //   10011 = MOVE
  //   10100 = LI
  //   10101 = LA
  //   10110 = LW
  //   10111 = SW
  //   OPPCODES:  
  //   00101 = DIV
  //   00110 = MFHI
endmodule

module cpu (
  input  in_1,
  input  [31:0] in_2,
  input  in_3,
  input  in_4,
  input  in_5,
  input  [31:0] in_6,
  output [31:0] out_7
);

  wire I, J, jr, Li;
  wire [4:0] OPPCODE, pc, pcadder_1_out_3, rd, rs, rt, sh;
  wire [31:0] A, ALUOUT, B, imm, oB, WriteData;

  OppDecoder oppdecoder_1 (
    .OPPIN(in_2), .oppcode(OPPCODE), .rs(rs), .rt(rt), .rd(rd), .sh(sh), .imm(imm), .LI(Li), .I(I), .J(J),
    .jr(jr));  // open: func, addr, Move, Branch, Shift, R
  Multiplexer #(.width(5), .enable("false")) multiplexer_1 (.in0(5'b00001), .sel(J));  // open: in1, out
  pcadder pcadder_1 (.pc(pc), .out_3(pcadder_1_out_3));  // open: b
  Multiplexer #(.width(5), .enable("false")) multiplexer_2 (.in0(pcadder_1_out_3), .out(pc));  // open: in1, sel
  RegisterFile registerfile_1 (
    .ReadSelectorA(rs), .CLK(in_1), .WriteEnable(in_1), .WriteSelector(rd), .WriteData(WriteData),
    .ReadSelectorB(rt), .DataOutputA(A), .DataOutputB(oB));
  RAM #(.addrWidth(5), .dataWidth(32), .databus("bibus")) ram_1 (
    .addr(pc), .we(in_3), .oe(in_4), .clk(in_5), .din(in_6), .dout(out_7));
  Multiplexer #(.width(32), .enable("false")) multiplexer_3 (.in0(oB), .in1(imm), .out(B), .sel(I));
  ALU alu_1 (.A(A), .B(B), .OPPCODE(OPPCODE), .S(sh), .Sign(1'b0), .R(ALUOUT));
  Multiplexer #(.width(32), .enable("false")) multiplexer_4 (.in0(ALUOUT), .in1(imm), .out(WriteData), .sel(Li));
endmodule

module OppDecoder (
  input  [31:0] OPPIN,
  output [4:0] oppcode,
  output [4:0] rs,
  output [4:0] rt,
  output [4:0] rd,
  output [4:0] sh,
  output [5:0] func,
  output [25:0] addr,
  output [31:0] imm,
  output LI,
  output Move,
  output I,
  output Branch,
  output J,
  output jr,
  output Shift,
  output R
);

  wire orrr_1_out_2, orrr_2_out_2;
  wire [15:0] or_5_out;
  wire [25:0] B0_out, demultiplexer_1_out1, demultiplexer_1_out2, demultiplexer_1_out3, demultiplexer_1_out4,
       demultiplexer_1_out5, demultiplexer_1_out6, demultiplexer_1_out7, demultiplexer_1_out8,
       demultiplexer_1_out9, demultiplexer_1_out10, demultiplexer_1_out11, demultiplexer_1_out12,
       demultiplexer_1_out13, demultiplexer_1_out14, demultiplexer_1_out15, demultiplexer_1_out16,
       demultiplexer_1_out17, demultiplexer_1_out18, demultiplexer_1_out19, demultiplexer_1_out20,
       demultiplexer_1_out21, demultiplexer_1_out22, demultiplexer_1_out23, I0_out;
  wire [25:11] R0_out;

  Demultiplexer #(.select(5), .width(26), .enable("false")) demultiplexer_1 (
    .out1(demultiplexer_1_out1), .out2(demultiplexer_1_out2), .out3(demultiplexer_1_out3),
    .out4(demultiplexer_1_out4), .out5(demultiplexer_1_out5), .out6(demultiplexer_1_out6),
    .out7(demultiplexer_1_out7), .out8(demultiplexer_1_out8), .out9(demultiplexer_1_out9),
    .out10(demultiplexer_1_out10), .out11(demultiplexer_1_out11), .out12(demultiplexer_1_out12),
    .out13(demultiplexer_1_out13), .out14(demultiplexer_1_out14), .out15(demultiplexer_1_out15),
    .out16(demultiplexer_1_out16), .out17(demultiplexer_1_out17), .out18(demultiplexer_1_out18),
    .out19(demultiplexer_1_out19), .out20(demultiplexer_1_out20), .out21(demultiplexer_1_out21),
    .out22(demultiplexer_1_out22), .out23(demultiplexer_1_out23), .in(OPPIN[25:0]), .sel(OPPIN[31:27]));  // open: out0, out24, out25, out26, out27, out28, out29, out30, out31
  orrr orrr_1 (.in_1(demultiplexer_1_out10), .out_2(orrr_1_out_2));
  orrr orrr_2 (.in_1(demultiplexer_1_out11), .out_2(orrr_2_out_2));
  or or_1 (Shift, orrr_1_out_2, orrr_2_out_2);
  orrr orrr_3 (.in_1(demultiplexer_1_out14), .out_2(jr));
  assign {R0_out, sh, func} = demultiplexer_1_out1 | demultiplexer_1_out3 | demultiplexer_1_out4 | demultiplexer_1_out5 | demultiplexer_1_out6 | demultiplexer_1_out14 | demultiplexer_1_out7 | demultiplexer_1_out8 | demultiplexer_1_out9 | demultiplexer_1_out10 | demultiplexer_1_out11;  // OR_Gate R0, 26 bits wide
  assign addr = demultiplexer_1_out12 | demultiplexer_1_out13;  // OR_Gate J0, 26 bits wide
  assign B0_out = demultiplexer_1_out15 | demultiplexer_1_out16 | demultiplexer_1_out17 | demultiplexer_1_out18;  // OR_Gate B0, 26 bits wide
  assign I0_out = demultiplexer_1_out2 | demultiplexer_1_out22 | demultiplexer_1_out23;  // OR_Gate I0, 26 bits wide
  orrr orrr_4 (.in_1(demultiplexer_1_out19), .out_2(Move));
  orrr orrr_5 (.in_1(I0_out), .out_2(I));
  orrr orrr_6 (.in_1(B0_out), .out_2(Branch));
  orrr orrr_7 (.in_1(addr), .out_2(J));
  orrr orrr_8 (.in_1({R0_out, sh, func}), .out_2(R));
  orrr orrr_9 (.in_1(demultiplexer_1_out20), .out_2(LI));
  assign rs = B0_out[25:21] | R0_out[25:21] | demultiplexer_1_out21[25:21] | I0_out[25:21] | demultiplexer_1_out19[25:21];  // OR_Gate or_2, 5 bits wide
  assign rt = B0_out[20:16] | R0_out[20:16] | I0_out[20:16] | demultiplexer_1_out19[20:16];  // OR_Gate or_3, 5 bits wide
  assign rd = R0_out[15:11] | demultiplexer_1_out20[25:21];  // OR_Gate or_4, 5 bits wide
  assign or_5_out = I0_out[15:0] | demultiplexer_1_out20[15:0] | B0_out[15:0];  // OR_Gate or_5, 16 bits wide
  assign imm = {{16{1'b0}}, or_5_out};  // Bit_Extender bit_extender_1

  assign oppcode = OPPIN[31:27];
endmodule

module orrr (
  input  [25:0] in_1,
  output out_2
);

  or or_1 (out_2, in_1[0], in_1[1], in_1[2], in_1[3], in_1[4], in_1[5], in_1[6], in_1[7], in_1[8], in_1[9], in_1[10], in_1[11], in_1[12], in_1[13], in_1[14], in_1[15], in_1[16], in_1[17], in_1[18], in_1[19], in_1[20], in_1[21], in_1[22], in_1[23], in_1[24], in_1[25]);
endmodule

module pcadder (
  input  [4:0] pc,
  input  [4:0] b,
  output [4:0] out_3
);

  wire fourbitadder_1_co;

  FourBitAdder fourbitadder_1 (
    .A0(pc[0]), .B0(b[0]), .A1(pc[1]), .B1(b[1]), .A2(pc[2]), .B2(b[2]), .A3(pc[3]), .B3(b[3]),
    .R0(out_3[0]), .R1(out_3[1]), .R2(out_3[2]), .R3(out_3[3]), .Co(fourbitadder_1_co));  // open: Ci
  FullAdder fulladder_1 (.Ci(fourbitadder_1_co), .A(pc[4]), .B(b[4]), .R(out_3[4]));  // open: Co
endmodule
